// Logisim project CRC.circ as structural Verilog
module CRC (
  input  [7:0] in_1,
  input  [3:0] in_2,
  output [10:0] out_3
);

  wire [2:0] mod2divide_2_out_3, mod2divide_3_out_3, mod2divide_4_out_3, mod2divide_5_out_3,
       mod2divide_6_out_3, mod2divide_7_out_3, mod2divide_8_out_3;

  mod2divide mod2divide_1 ();  // open: in_1, in_2, out_3
  mod2divide mod2divide_2 (.in_1(in_1[7:4]), .in_2(in_2), .out_3(mod2divide_2_out_3));
  mod2divide mod2divide_3 (.in_1({mod2divide_2_out_3, in_1[3]}), .in_2(in_2), .out_3(mod2divide_3_out_3));
  mod2divide mod2divide_4 (.in_1({mod2divide_3_out_3, in_1[2]}), .in_2(in_2), .out_3(mod2divide_4_out_3));
  // Probe on mod2divide_5_out_3
  mod2divide mod2divide_5 (.in_1({mod2divide_4_out_3, in_1[1]}), .in_2(in_2), .out_3(mod2divide_5_out_3));
  mod2divide mod2divide_6 (.in_1({mod2divide_5_out_3, in_1[0]}), .in_2(in_2), .out_3(mod2divide_6_out_3));
  mod2divide mod2divide_7 (.in_1({mod2divide_6_out_3, 1'b0}), .in_2(in_2), .out_3(mod2divide_7_out_3));
  mod2divide mod2divide_8 (.in_1({mod2divide_7_out_3, 1'b0}), .in_2(in_2), .out_3(mod2divide_8_out_3));
  mod2divide mod2divide_9 (.in_1({mod2divide_8_out_3, 1'b0}), .in_2(in_2), .out_3(out_3[2:0]));

  assign out_3[10:3] = in_1;

  // Other names for the same wires on the sheet: data[7:0] = in_1; output[10:0] = {in_1, out_3[2:0]};
  //   divisor[3:0] = in_2; validation[2:0] = out_3[2:0]
endmodule

module mod2divide (
  input  [3:0] in_1,
  input  [3:0] in_2,
  output [2:0] out_3
);

  wire [3:0] xor_1_out;
  wire [3:3] multiplexer_1_out;

  assign xor_1_out = in_1 ^ in_2;  // XOR_Gate xor_1, 4 bits wide
  Multiplexer #(.width(4), .enable("false")) multiplexer_1 (
    .in0(in_1), .in1(xor_1_out), .out({multiplexer_1_out[3], out_3}), .sel(in_1[3]));

  // Other names for the same wires on the sheet: select = in_1[3]
endmodule
