// Logisim project grf.circ as structural Verilog
module grf (
  input  in_1,
  input  in_2,
  input  in_3,
  input  [4:0] in_4,
  input  [4:0] in_5,
  input  [4:0] in_6,
  input  [31:0] in_7,
  output [31:0] out_8,
  output [31:0] out_9
);

  wire WE0, WE1, WE2, WE3, WE4, WE5, WE6, WE7, WE8, WE9, WE10, WE11, WE12, WE13, WE14, WE15, WE16, WE17,
       WE18, WE19, WE20, WE21, WE22, WE23, WE24, WE25, WE26, WE27, WE28, WE29, WE30, WE31;
  wire [4:0] multiplexer_1_out;
  wire [31:0] In_0, In_1_t, In_2_t, In_3_t, In_4_t, In_5_t, In_6_t, In_7_t, In_8, In_9, In_10, In_11, In_12,
       In_13, In_14, In_15, In_16, In_17, In_18, In_19, In_20, In_21, In_22, In_23, In_24, In_25, In_26,
       In_27, In_28, In_29, In_30, In_31, result0, result1, result2, result3, result4, result5, result6,
       result7, result8, result9, result10, result11, result12, result13, result14, result15, result16,
       result17, result18, result19, result20, result21, result22, result23, result24, result25, result26,
       result27, result28, result29, result30, result31;

  Register #(.width(32)) register_1 (.en(WE0), .Q(result0), .clk(in_1), .clr(in_2));  // open: D
  Register #(.width(32)) register_2 (.D(In_8), .en(WE8), .Q(result8), .clk(in_1), .clr(in_2));
  Register #(.width(32)) register_3 (.D(In_16), .en(WE16), .Q(result16), .clk(in_1), .clr(in_2));
  Register #(.width(32)) register_4 (.D(In_24), .en(WE24), .Q(result24), .clk(in_1), .clr(in_2));
  Demultiplexer #(.select(5), .width(32), .enable("false")) demultiplexer_1 (
    .out0(In_0), .out1(In_1_t), .out2(In_2_t), .out3(In_3_t), .out4(In_4_t), .out5(In_5_t), .out6(In_6_t),
    .out7(In_7_t), .out8(In_8), .out9(In_9), .out10(In_10), .out11(In_11), .out12(In_12), .out13(In_13),
    .out14(In_14), .out15(In_15), .out16(In_16), .out17(In_17), .out18(In_18), .out19(In_19), .out20(In_20),
    .out21(In_21), .out22(In_22), .out23(In_23), .out24(In_24), .out25(In_25), .out26(In_26), .out27(In_27),
    .out28(In_28), .out29(In_29), .out30(In_30), .out31(In_31), .in(in_7), .sel(in_6));
  Register #(.width(32)) register_5 (.D(In_1_t), .en(WE1), .Q(result1), .clk(in_1), .clr(in_2));
  Register #(.width(32)) register_6 (.D(In_9), .en(WE9), .Q(result9), .clk(in_1), .clr(in_2));
  Register #(.width(32)) register_7 (.D(In_17), .en(WE17), .Q(result17), .clk(in_1), .clr(in_2));
  Register #(.width(32)) register_8 (.D(In_25), .en(WE25), .Q(result25), .clk(in_1), .clr(in_2));
  Decoder #(.select(5), .enable("false")) decoder_1 (
    .out0(WE0), .out1(WE1), .out2(WE2), .out3(WE3), .out4(WE4), .out5(WE5), .out6(WE6), .out7(WE7),
    .out8(WE8), .out9(WE9), .out10(WE10), .out11(WE11), .out12(WE12), .out13(WE13), .out14(WE14),
    .out15(WE15), .out16(WE16), .out17(WE17), .out18(WE18), .out19(WE19), .out20(WE20), .out21(WE21),
    .out22(WE22), .out23(WE23), .out24(WE24), .out25(WE25), .out26(WE26), .out27(WE27), .out28(WE28),
    .out29(WE29), .out30(WE30), .out31(WE31), .sel(multiplexer_1_out));
  Multiplexer #(.width(5), .enable("false")) multiplexer_1 (
    .in0({5{1'b0}}), .in1(in_6), .out(multiplexer_1_out), .sel(in_3));
  Register #(.width(32)) register_9 (.D(In_2_t), .en(WE2), .Q(result2), .clk(in_1), .clr(in_2));
  Register #(.width(32)) register_10 (.D(In_10), .en(WE10), .Q(result10), .clk(in_1), .clr(in_2));
  Register #(.width(32)) register_11 (.D(In_18), .en(WE18), .Q(result18), .clk(in_1), .clr(in_2));
  Register #(.width(32)) register_12 (.D(In_26), .en(WE26), .Q(result26), .clk(in_1), .clr(in_2));
  Multiplexer #(.select(5), .width(32), .enable("false")) multiplexer_2 (
    .in0(result0), .in1(result1), .in2(result2), .in3(result3), .in4(result4), .in5(result5), .in6(result6),
    .in7(result7), .in8(result8), .in9(result9), .in10(result10), .in11(result11), .in12(result12),
    .in13(result13), .in14(result14), .in15(result15), .in16(result16), .in17(result17), .in18(result18),
    .in19(result19), .in20(result20), .in21(result21), .in22(result22), .in23(result23), .in24(result24),
    .in25(result25), .in26(result26), .in27(result27), .in28(result28), .in29(result29), .in30(result30),
    .in31(result31), .out(out_8), .sel(in_4));
  Register #(.width(32)) register_13 (.D(In_3_t), .en(WE3), .Q(result3), .clk(in_1), .clr(in_2));
  Register #(.width(32)) register_14 (.D(In_11), .en(WE11), .Q(result11), .clk(in_1), .clr(in_2));
  Register #(.width(32)) register_15 (.D(In_19), .en(WE19), .Q(result19), .clk(in_1), .clr(in_2));
  Register #(.width(32)) register_16 (.D(In_27), .en(WE27), .Q(result27), .clk(in_1), .clr(in_2));
  Multiplexer #(.select(5), .width(32), .enable("false")) multiplexer_3 (
    .in0(result0), .in1(result1), .in2(result2), .in3(result3), .in4(result4), .in5(result5), .in6(result6),
    .in7(result7), .in8(result8), .in9(result9), .in10(result10), .in11(result11), .in12(result12),
    .in13(result13), .in14(result14), .in15(result15), .in16(result16), .in17(result17), .in18(result18),
    .in19(result19), .in20(result20), .in21(result21), .in22(result22), .in23(result23), .in24(result24),
    .in25(result25), .in26(result26), .in27(result27), .in28(result28), .in29(result29), .in30(result30),
    .in31(result31), .out(out_9), .sel(in_5));
  Register #(.width(32)) register_17 (.D(In_4_t), .en(WE4), .Q(result4), .clk(in_1), .clr(in_2));
  Register #(.width(32)) register_18 (.D(In_12), .en(WE12), .Q(result12), .clk(in_1), .clr(in_2));
  Register #(.width(32)) register_19 (.D(In_20), .en(WE20), .Q(result20), .clk(in_1), .clr(in_2));
  Register #(.width(32)) register_20 (.D(In_28), .en(WE28), .Q(result28), .clk(in_1), .clr(in_2));
  Register #(.width(32)) register_21 (.D(In_5_t), .en(WE5), .Q(result5), .clk(in_1), .clr(in_2));
  Register #(.width(32)) register_22 (.D(In_13), .en(WE13), .Q(result13), .clk(in_1), .clr(in_2));
  Register #(.width(32)) register_23 (.D(In_21), .en(WE21), .Q(result21), .clk(in_1), .clr(in_2));
  Register #(.width(32)) register_24 (.D(In_29), .en(WE29), .Q(result29), .clk(in_1), .clr(in_2));
  Register #(.width(32)) register_25 (.D(In_6_t), .en(WE6), .Q(result6), .clk(in_1), .clr(in_2));
  Register #(.width(32)) register_26 (.D(In_14), .en(WE14), .Q(result14), .clk(in_1), .clr(in_2));
  Register #(.width(32)) register_27 (.D(In_22), .en(WE22), .Q(result22), .clk(in_1), .clr(in_2));
  Register #(.width(32)) register_28 (.D(In_30), .en(WE30), .Q(result30), .clk(in_1), .clr(in_2));
  Register #(.width(32)) register_29 (.D(In_7_t), .en(WE7), .Q(result7), .clk(in_1), .clr(in_2));
  Register #(.width(32)) register_30 (.D(In_15), .en(WE15), .Q(result15), .clk(in_1), .clr(in_2));
  Register #(.width(32)) register_31 (.D(In_23), .en(WE23), .Q(result23), .clk(in_1), .clr(in_2));
  Register #(.width(32)) register_32 (.D(In_31), .en(WE31), .Q(result31), .clk(in_1), .clr(in_2));

  // Other names for the same wires on the sheet: A1[4:0] = in_4; A2[4:0] = in_5; A3[4:0] = in_6; CLK = in_1;
  //   RD1[31:0] = out_8; RD2[31:0] = out_9; Reset = in_2; WD[31:0] = in_7; WE = in_3
endmodule
