// Logisim project fsm.circ as structural Verilog
module fsm (
  input  [1:0] in_1,
  input  in_2,
  input  in_3,
  output out_4
);

  wire calculate_num;
  wire [1:0] multiplexer_4_out, multiplexer_5_out, now_state, S_0, S_1, S_2;

  Comparator #(.width(2), .mode("unsigned")) comparator_1 (.a(in_1), .b(2'b01), .eq(calculate_num));  // open: gt, lt
  Multiplexer #(.select(2), .width(2), .enable("false")) multiplexer_1 (
    .in0(2'b00), .in1(2'b01), .in2(2'b00), .in3(2'b00), .out(S_0), .sel(in_1));
  Multiplexer #(.select(2), .width(2), .enable("false")) multiplexer_2 (
    .in0(2'b10), .in1(2'b01), .in2(2'b10), .in3(2'b00), .out(S_1), .sel(in_1));
  Multiplexer #(.select(2), .width(2), .enable("false")) multiplexer_3 (
    .in0(2'b00), .in1(2'b01), .in2(2'b00), .in3(2'b00), .out(S_2), .sel(in_1));
  Multiplexer #(.select(2), .width(2), .enable("false")) multiplexer_4 (
    .in0(S_0), .in1(S_1), .in2(S_2), .out(multiplexer_4_out), .sel(now_state));  // open: in3
  Multiplexer #(.width(2), .enable("false")) multiplexer_5 (
    .in0(multiplexer_4_out), .in1(2'b00), .out(multiplexer_5_out), .sel(in_2));
  Register #(.width(2)) register_1 (.D(multiplexer_5_out), .Q(now_state), .clk(in_3));  // open: en, clr
  \output  output_1 (.now_state(now_state), .CLR(in_2), .In(in_1), .out_4(out_4));

  // Other names for the same wires on the sheet: CLK = in_3; CLR = in_2; In[1:0] = in_1; Z = out_4

  // Notes on the sheet:
  //   S_0
  //   S_1
  //   S_2
endmodule

module \output  (
  input  [1:0] now_state,
  input  CLR,
  input  [1:0] In,
  output out_4
);

  wire comparator_1_eq, comparator_2_eq, comparator_3_eq, not_1_out, or_1_out;

  Comparator #(.width(2), .mode("unsigned")) comparator_1 (
    .a(now_state), .b(2'b10), .eq(comparator_1_eq));  // open: gt, lt
  Comparator #(.width(2), .mode("unsigned")) comparator_2 (.a(2'b00), .b(In), .eq(comparator_2_eq));  // open: gt, lt
  or or_1 (or_1_out, comparator_2_eq, comparator_3_eq);
  Comparator #(.width(2), .mode("unsigned")) comparator_3 (.a(2'b10), .b(In), .eq(comparator_3_eq));  // open: gt, lt
  and and_1 (out_4, comparator_1_eq, not_1_out, or_1_out);
  not not_1 (not_1_out, CLR);
endmodule

module backup (
  input  [1:0] in_1,
  input  in_2,
  input  in_3,
  output out_4
);

  wire calculate_num, check_b, reset_b;
  wire [1:0] buffer, multiplexer_1_out, multiplexer_2_out, multiplexer_6_out, multiplexer_7_out, now_state,
       register_1_q, S_0, S_1, S_2;

  Comparator #(.width(2), .mode("unsigned")) comparator_1 (.a(in_1), .b(2'b01), .eq(calculate_num));  // open: gt, lt
  Multiplexer #(.width(2), .enable("false")) multiplexer_1 (
    .in0(2'b01), .in1(2'b00), .out(multiplexer_1_out), .sel(check_b));
  Multiplexer #(.width(2), .enable("false")) multiplexer_2 (
    .in0(2'b00), .in1(buffer), .out(multiplexer_2_out), .sel(calculate_num));
  Multiplexer #(.select(2), .width(2), .enable("false")) multiplexer_3 (
    .in0(2'b00), .in1(2'b01), .in2(2'b00), .in3(2'b00), .out(S_0), .sel(in_1));
  Multiplexer #(.select(2), .width(2), .enable("false")) multiplexer_4 (
    .in0(2'b10), .in1(multiplexer_1_out), .in2(2'b10), .in3(2'b00), .out(S_1), .sel(in_1));
  Multiplexer #(.select(2), .width(2), .enable("false")) multiplexer_5 (
    .in0(2'b00), .in1(2'b01), .in2(2'b00), .in3(2'b00), .out(S_2), .sel(in_1));
  Multiplexer #(.select(2), .width(2), .enable("false")) multiplexer_6 (
    .in0(S_0), .in1(S_1), .in2(S_2), .out(multiplexer_6_out), .sel(now_state));  // open: in3
  Multiplexer #(.width(2), .enable("false")) multiplexer_7 (
    .in0(multiplexer_6_out), .in1(2'b00), .out(multiplexer_7_out), .sel(in_2));
  Register #(.width(2)) register_1 (.D(multiplexer_2_out), .Q(register_1_q), .clk(in_3), .clr(reset_b));  // open: en
  Register #(.width(2)) register_2 (.D(multiplexer_7_out), .Q(now_state), .clk(in_3));  // open: en, clr
  Comparator #(.width(2), .mode("unsigned")) comparator_2 (.a(2'b10), .b(register_1_q), .lt(reset_b));  // open: gt, eq
  Adder #(.width(2)) adder_1 (.a(register_1_q), .b(2'b01), .out(buffer));  // open: cin, cout
  \output  output_1 (.now_state(now_state), .CLR(in_2), .In(in_1), .out_4(out_4));
  Comparator #(.width(2), .mode("unsigned")) comparator_3 (.a(2'b10), .b(buffer), .lt(check_b));  // open: gt, eq

  // Other names for the same wires on the sheet: CLK = in_3; CLR = in_2; In[1:0] = in_1; Z = out_4

  // Notes on the sheet:
  //   S_0
  //   S_1
  //   S_2
endmodule
