// Logisim project navigation.circ as structural Verilog
// x
module navigation (
  input  [1:0] in_1,
  input  in_2,
  input  in_3,
  output out_4,
  output out_5
);

  wire East, multiplexer_7_out, North, or_1_out, or_2_out, pass, South, West;
  wire [2:0] adder_1_out, adder_2_out, multiplexer_1_out, multiplexer_2_out, multiplexer_3_out,
       multiplexer_4_out, multiplexer_5_out, multiplexer_6_out, next_x, next_y, subtractor_1_out,
       subtractor_2_out, x, y;

  Decoder #(.select(2), .enable("false")) decoder_1 (.out0(North), .out1(East), .out2(South), .out3(West), .sel(in_1));
  Adder #(.width(3)) adder_1 (.a(y), .b(3'b001), .out(adder_1_out));  // open: cin, cout
  Subtractor #(.width(3)) subtractor_1 (.a(y), .b(3'b001), .out(subtractor_1_out));  // open: bin, bout
  Adder #(.width(3)) adder_2 (.a(x), .b(3'b001), .out(adder_2_out));  // open: cin, cout
  Subtractor #(.width(3)) subtractor_2 (.a(x), .b(3'b001), .out(subtractor_2_out));  // open: bin, bout
  assign next_y = North ? adder_1_out : 3'bz;  // Controlled_Buffer controlled_buffer_1
  assign next_y = South ? subtractor_1_out : 3'bz;  // Controlled_Buffer controlled_buffer_2
  assign next_x = East ? adder_2_out : 3'bz;  // Controlled_Buffer controlled_buffer_3
  assign next_x = West ? subtractor_2_out : 3'bz;  // Controlled_Buffer controlled_buffer_4
  or or_1 (or_1_out, West, East);
  Multiplexer #(.width(3), .enable("false")) multiplexer_1 (
    .in0(x), .in1(next_x), .out(multiplexer_1_out), .sel(or_1_out));
  Multiplexer #(.width(3), .enable("false")) multiplexer_2 (
    .in0(y), .in1(next_y), .out(multiplexer_2_out), .sel(or_2_out));
  or or_2 (or_2_out, North, South);
  Multiplexer #(.width(3), .enable("false")) multiplexer_3 (.in0(next_y), .in1(y), .out(multiplexer_3_out), .sel(pass));
  Multiplexer #(.width(3), .enable("false")) multiplexer_4 (.in0(next_x), .in1(x), .out(multiplexer_4_out), .sel(pass));
  wall wall_1 (.x(multiplexer_1_out), .y(multiplexer_2_out), .out_3(pass));
  Multiplexer #(.width(3), .enable("false")) multiplexer_5 (
    .in0(multiplexer_3_out), .in1(3'b000), .out(multiplexer_5_out), .sel(out_4));
  Register #(.width(3)) Vertical (.D(multiplexer_5_out), .Q(y), .clk(in_2), .clr(in_3));  // open: en
  Multiplexer #(.width(3), .enable("false")) multiplexer_6 (
    .in0(multiplexer_4_out), .in1(3'b000), .out(multiplexer_6_out), .sel(out_4));
  Register #(.width(3)) Horizontal (.D(multiplexer_6_out), .Q(x), .clk(in_2), .clr(in_3));  // open: en
  Multiplexer #(.enable("false")) multiplexer_7 (.in0(pass), .in1(1'b0), .out(multiplexer_7_out), .sel(out_4));
  \end  end_1 (.in_1(x), .in_2(y), .out_3(out_4));
  Register #(.width(1)) register_1 (.D(multiplexer_7_out), .Q(out_5), .clk(in_2), .clr(in_3));  // open: en

  // Other names for the same wires on the sheet: arrive = out_4; clk = in_2; dir[1:0] = in_1; hit = out_5;
  //   reset = in_3
endmodule

module wall (
  input  [2:0] x,
  input  [2:0] y,
  output out_3
);

  wire and_1_out, comparator_1_lt, comparator_2_eq, comparator_3_eq, comparator_4_gt, comparator_5_lt,
       comparator_6_gt;

  Comparator #(.width(3)) comparator_1 (.a(x), .b(3'b000), .lt(comparator_1_lt));  // open: gt, eq
  Comparator #(.width(3)) comparator_2 (.a(x), .b(3'b001), .eq(comparator_2_eq));  // open: gt, lt
  Comparator #(.width(3)) comparator_3 (.a(y), .b(3'b000), .eq(comparator_3_eq));  // open: gt, lt
  Comparator #(.width(3)) comparator_4 (.a(y), .b(3'b010), .gt(comparator_4_gt));  // open: eq, lt
  Comparator #(.width(3)) comparator_5 (.a(y), .b(3'b000), .lt(comparator_5_lt));  // open: gt, eq
  Comparator #(.width(3)) comparator_6 (.a(x), .b(3'b001), .gt(comparator_6_gt));  // open: eq, lt
  and and_1 (and_1_out, comparator_2_eq, comparator_3_eq);
  or or_1 (out_3, comparator_1_lt, and_1_out, comparator_4_gt, comparator_5_lt, comparator_6_gt);
endmodule

module \end  (
  input  [2:0] in_1,
  input  [2:0] in_2,
  output out_3
);

  wire comparator_1_eq, comparator_2_eq;

  Comparator #(.width(3)) comparator_1 (.a(in_1), .b(3'b001), .eq(comparator_1_eq));  // open: gt, lt
  and and_1 (out_3, comparator_1_eq, comparator_2_eq);
  Comparator #(.width(3)) comparator_2 (.a(in_2), .b(3'b010), .eq(comparator_2_eq));  // open: gt, lt
endmodule

module navigation_backup (
  input  [1:0] in_1,
  input  in_2,
  input  in_3,
  output out_4,
  output out_5
);

  wire East, North, or_1_out, or_2_out, South, West;
  wire [2:0] adder_1_out, adder_2_out, multiplexer_1_out, multiplexer_2_out, multiplexer_3_out,
       multiplexer_4_out, multiplexer_5_out, multiplexer_6_out, next_x, next_y, subtractor_1_out,
       subtractor_2_out, x, y;

  Decoder #(.select(2), .enable("false")) decoder_1 (.out0(North), .out1(East), .out2(South), .out3(West), .sel(in_1));
  Adder #(.width(3)) adder_1 (.a(y), .b(3'b001), .out(adder_1_out));  // open: cin, cout
  Subtractor #(.width(3)) subtractor_1 (.a(y), .b(3'b001), .out(subtractor_1_out));  // open: bin, bout
  Adder #(.width(3)) adder_2 (.a(x), .b(3'b001), .out(adder_2_out));  // open: cin, cout
  Subtractor #(.width(3)) subtractor_2 (.a(x), .b(3'b001), .out(subtractor_2_out));  // open: bin, bout
  assign next_y = North ? adder_1_out : 3'bz;  // Controlled_Buffer controlled_buffer_1
  assign next_y = South ? subtractor_1_out : 3'bz;  // Controlled_Buffer controlled_buffer_2
  assign next_x = East ? adder_2_out : 3'bz;  // Controlled_Buffer controlled_buffer_3
  assign next_x = West ? subtractor_2_out : 3'bz;  // Controlled_Buffer controlled_buffer_4
  or or_1 (or_1_out, West, East);
  Multiplexer #(.width(3), .enable("false")) multiplexer_1 (
    .in0(x), .in1(next_x), .out(multiplexer_1_out), .sel(or_1_out));
  Multiplexer #(.width(3), .enable("false")) multiplexer_2 (
    .in0(y), .in1(next_y), .out(multiplexer_2_out), .sel(or_2_out));
  or or_2 (or_2_out, North, South);
  Multiplexer #(.width(3), .enable("false")) multiplexer_3 (
    .in0(next_y), .in1(y), .out(multiplexer_3_out), .sel(out_5));
  Multiplexer #(.width(3), .enable("false")) multiplexer_4 (
    .in0(next_x), .in1(x), .out(multiplexer_4_out), .sel(out_5));
  wall wall_1 (.x(multiplexer_1_out), .y(multiplexer_2_out), .out_3(out_5));
  Register #(.width(3)) Vertical (.D(multiplexer_5_out), .Q(y), .clk(in_2), .clr(in_3));  // open: en
  Multiplexer #(.width(3), .enable("false")) multiplexer_5 (
    .in0(multiplexer_3_out), .in1(3'b000), .out(multiplexer_5_out), .sel(out_4));
  Register #(.width(3)) Horizontal (.D(multiplexer_6_out), .Q(x), .clk(in_2), .clr(in_3));  // open: en
  Multiplexer #(.width(3), .enable("false")) multiplexer_6 (
    .in0(multiplexer_4_out), .in1(3'b000), .out(multiplexer_6_out), .sel(out_4));
  \end  end_1 (.in_1(x), .in_2(y), .out_3(out_4));

  // Other names for the same wires on the sheet: arrive = out_4; clk = in_2; dir[1:0] = in_1; hit = out_5;
  //   pass = out_5; reset = in_3
endmodule
