// Logisim project ftoi.circ as structural Verilog: 4 circuits, main circuit main
module main (
);

  // AND_Gate and_1 is placed but not wired
endmodule

module ftoi (
  input  [15:0] in_1,
  output [31:0] out_2
);

  wire comparator_1_eq, comparator_2_eq;
  wire [31:0] float2int_1_out_4, multiplexer_1_out;

  float2int float2int_1 (.in_1(in_1[15]), .in_2(in_1[14:10]), .in_3(in_1[9:0]), .out_4(float2int_1_out_4));
  Comparator #(.width(5)) comparator_1 (.a({5{1'b0}}), .b(in_1[14:10]), .eq(comparator_1_eq));  // open: gt, lt
  Multiplexer #(.width(32), .enable("false")) multiplexer_1 (
    .in0(float2int_1_out_4), .in1({32{1'b0}}), .out(multiplexer_1_out), .sel(comparator_1_eq));
  Multiplexer #(.width(32), .enable("false")) multiplexer_2 (
    .in0(multiplexer_1_out), .in1({32{1'b0}}), .out(out_2), .sel(comparator_2_eq));
  Comparator #(.width(5)) comparator_2 (.a({5{1'b1}}), .b(in_1[14:10]), .eq(comparator_2_eq));  // open: gt, lt

  // Other names for the same wires on the sheet: float[15:0] = in_1; mantissa[9:0] = in_1[9:0];
  //   exponent[4:0] = in_1[14:10]; sign = in_1[15]; int[31:0] = out_2
endmodule

module float2int (
  input  in_1,
  input  [4:0] in_2,
  input  [9:0] in_3,
  output [31:0] out_4
);

  wire comparator_1_eq, comparator_1_gt, flag;
  wire [4:0] subtractor_1_out, subtractor_2_out, true_exponent;
  wire [31:0] multiplexer_2_out, n32bitscomplement_1_out_2, shifter_1_out, shifter_2_out, true_mantissa;

  Subtractor #(.width(5)) subtractor_1 (.a(5'b11001), .b(in_2), .out(subtractor_1_out));  // open: bin, bout
  Subtractor #(.width(5)) subtractor_2 (.a(in_2), .b(5'b11001), .out(subtractor_2_out));  // open: bin, bout
  assign true_mantissa = {{21{1'b0}}, {1'b1, in_3}};  // Bit_Extender bit_extender_1
  Multiplexer #(.width(5), .enable("false")) multiplexer_1 (
    .in0(subtractor_1_out), .in1(subtractor_2_out), .out(true_exponent), .sel(flag));
  // Probe on true_exponent
  Shifter #(.width(32), .shift("lr")) shifter_1 (.in(true_mantissa), .\dist (true_exponent), .out(shifter_1_out));
  Multiplexer #(.width(32), .enable("false")) multiplexer_2 (
    .in0(shifter_1_out), .in1(shifter_2_out), .out(multiplexer_2_out), .sel(flag));
  Shifter #(.width(32)) shifter_2 (.in(true_mantissa), .\dist (true_exponent), .out(shifter_2_out));
  or or_1 (flag, comparator_1_gt, comparator_1_eq);
  Comparator #(.width(5), .mode("unsigned")) comparator_1 (
    .a(in_2), .b(5'b11001), .gt(comparator_1_gt), .eq(comparator_1_eq));  // open: lt
  _32bitscomplement u_32bitscomplement_1 (.in_1(multiplexer_2_out), .out_2(n32bitscomplement_1_out_2));
  Multiplexer #(.width(32), .enable("false")) multiplexer_3 (
    .in0(multiplexer_2_out), .in1(n32bitscomplement_1_out_2), .out(out_4), .sel(in_1));

  // Other names for the same wires on the sheet: mantissa[9:0] = in_3; exponent[4:0] = in_2; out[31:0] = out_4;
  //   sign = in_1
endmodule

module _32bitscomplement (
  input  [31:0] in_1,
  output [31:0] out_2
);

  wire [31:0] not_1_out;

  assign not_1_out = ~in_1;  // NOT_Gate not_1, 32 bits wide
  Adder #(.width(32)) adder_1 (.a(not_1_out), .b(32'h1), .out(out_2));  // open: cin, cout
endmodule
