// Logisim project arithmetic_right_shifter.circ as structural Verilog: 2 circuits, main circuit main
module main (
  input  [15:0] in_1,
  input  [3:0] in_2,
  output [15:0] out_3
);

  wire [15:0] divider_1_out, multiplexer_1_out, n2_power_1_out_2, not_1_out, not_2_out;

  // Probe on multiplexer_1_out
  Multiplexer #(.width(16), .enable("false")) multiplexer_1 (
    .in0(in_1), .in1(not_1_out), .out(multiplexer_1_out), .sel(in_1[15]));
  assign not_1_out = ~in_1;  // NOT_Gate not_1, 16 bits wide
  _2_power u_2_power_1 (.in_1(in_2), .out_2(n2_power_1_out_2));
  // Probe on divider_1_out
  Divider #(.width(16)) divider_1 (
    .a(multiplexer_1_out), .b(n2_power_1_out_2), .out(divider_1_out));  // open: upper, rem
  Multiplexer #(.width(16), .enable("false")) multiplexer_2 (
    .in0(divider_1_out), .in1(not_2_out), .out(out_3), .sel(in_1[15]));
  assign not_2_out = ~divider_1_out;  // NOT_Gate not_2, 16 bits wide
endmodule

module _2_power (
  input  [3:0] in_1,
  output [15:0] out_2
);

  Decoder #(.select(4), .enable("false")) decoder_1 (
    .out0(out_2[0]), .out1(out_2[1]), .out2(out_2[2]), .out3(out_2[3]), .out4(out_2[4]), .out5(out_2[5]),
    .out6(out_2[6]), .out7(out_2[7]), .out8(out_2[8]), .out9(out_2[9]), .out10(out_2[10]), .out11(out_2[11]),
    .out12(out_2[12]), .out13(out_2[13]), .out14(out_2[14]), .out15(out_2[15]), .sel(in_1));
endmodule
