// Logisim project vending_machine.circ as structural Verilog: 2 circuits, main circuit main
module main (
  input  [1:0] in_1,
  input  in_2,
  output out_3,
  output out_4,
  output out_5,
  output out_6
);

  wire clk, comparator_1_eq, comparator_1_gt;
  wire [3:0] adder_1_out, balance, multiplexer_1_out, multiplexer_2_out;

  Clock clock_1 (.out(clk));
  Multiplexer #(.select(2), .width(4), .enable("false")) multiplexer_1 (
    .in0(4'b0000), .in1(4'b0001), .in2(4'b0010), .in3(4'b0101), .out(multiplexer_1_out), .sel(in_1));
  change change_1 (.in_1(balance), .out_2(out_4), .out_3(out_5), .out_4(out_6));
  Adder #(.width(4)) adder_1 (.a(balance), .b(multiplexer_1_out), .out(adder_1_out));  // open: cin, cout
  or or_1 (out_3, comparator_1_gt, comparator_1_eq);
  Comparator #(.width(4), .mode("unsigned")) comparator_1 (
    .a(balance), .b(4'b0101), .gt(comparator_1_gt), .eq(comparator_1_eq));  // open: lt
  Multiplexer #(.width(4), .enable("false")) multiplexer_2 (
    .in0(adder_1_out), .in1(4'b0000), .out(multiplexer_2_out), .sel(out_3));
  Register #(.width(4)) register_1 (.D(multiplexer_2_out), .Q(balance), .clk(clk), .clr(in_2));  // open: en

  // Other names for the same wires on the sheet: dispense = out_3; money[1:0] = in_1; reset = in_2; return1 = out_4;
  //   return2 = out_5; return4 = out_6
endmodule

module change (
  input  [3:0] in_1,
  output out_2,
  output out_3,
  output out_4
);

  wire _1, _2, _4, _5, bit_extender_1_out;
  wire [3:0] divider_1_out, divider_2_out, divider_3_out, multiplexer_2_out, multiplexer_3_out,
       subtractor_1_out, subtractor_2_out;

  Subtractor #(.width(4)) subtractor_1 (.a(in_1), .b(4'b0101), .out(subtractor_1_out), .bout(_5));  // open: bin
  Divider #(.width(4)) divider_1 (.a(subtractor_1_out), .b(4'b0010), .out(divider_1_out));  // open: upper, rem
  Bit_Extender #(.in_width(4), .out_width(1)) bit_extender_1 (.in(divider_1_out), .out(bit_extender_1_out));
  Divider #(.width(4)) divider_2 (.a(subtractor_1_out), .b(4'b0100), .out(divider_2_out));  // open: upper, rem
  Bit_Extender #(.in_width(4), .out_width(1)) bit_extender_2 (.in(divider_2_out), .out(_4));
  Subtractor #(.width(4)) subtractor_2 (.a(subtractor_1_out), .b(4'b0010), .out(subtractor_2_out));  // open: bin, bout
  Multiplexer #(.enable("false")) multiplexer_1 (.in0(bit_extender_1_out), .in1(1'b0), .out(_2), .sel(_4));
  Multiplexer #(.width(4), .enable("false")) multiplexer_2 (
    .in0(subtractor_1_out), .in1(subtractor_2_out), .out(multiplexer_2_out), .sel(_2));
  Multiplexer #(.width(4), .enable("false")) multiplexer_3 (
    .in0(multiplexer_2_out), .in1(4'b0000), .out(multiplexer_3_out), .sel(_4));
  Divider #(.width(4)) divider_3 (.a(multiplexer_3_out), .b(4'b0001), .out(divider_3_out));  // open: upper, rem
  Multiplexer #(.enable("false")) multiplexer_4 (.in0(_1), .in1(1'b0), .out(out_2), .sel(_5));
  Multiplexer #(.enable("false")) multiplexer_5 (.in0(_2), .in1(1'b0), .out(out_3), .sel(_5));
  Multiplexer #(.enable("false")) multiplexer_6 (.in0(_4), .in1(1'b0), .out(out_4), .sel(_5));
  Bit_Extender #(.in_width(4), .out_width(1)) bit_extender_3 (.in(divider_3_out), .out(_1));
endmodule
