// Logisim project binary_string_process.circ as structural Verilog: 2 circuits, main circuit main
module main (
  input  [31:0] in_1,
  output [31:0] out_2
);

  wire comparator_1_eq;
  wire [4:0] bitfinder_1_index, n, subtractor_1_out;
  wire [31:0] bit_extender_1_out, or_1_out, process_u_1_out_3, shifter_1_out;

  // Probe on bitfinder_1_index
  BitFinder #(.width(32), .\type ("high1")) bitfinder_1 (.in(in_1), .index(bitfinder_1_index));  // open: found
  Shifter #(.width(32)) shifter_1 (.in(in_1), .\dist (5'b00101), .out(shifter_1_out));
  assign bit_extender_1_out = {{27{1'b0}}, n};  // Bit_Extender bit_extender_1
  Adder #(.width(5)) adder_1 (.a(5'b00001), .b(subtractor_1_out), .out(n));  // open: cin, cout
  Subtractor #(.width(5)) subtractor_1 (
    .a(bitfinder_1_index), .b(5'b00101), .out(subtractor_1_out));  // open: bin, bout
  assign or_1_out = shifter_1_out | bit_extender_1_out;  // OR_Gate or_1, 32 bits wide
  // Probe on n
  process_u process_u_1 (.in_1(in_1), .in_2(n), .out_3(process_u_1_out_3));
  Multiplexer #(.width(32), .enable("false")) multiplexer_1 (
    .in0(process_u_1_out_3), .in1(or_1_out), .out(out_2), .sel(comparator_1_eq));
  Comparator #(.width(5), .mode("unsigned")) comparator_1 (.a(5'b11011), .b(n), .eq(comparator_1_eq));  // open: gt, lt

  // Other names for the same wires on the sheet: input[31:0] = in_1; output[31:0] = out_2
endmodule

module process_u (
  input  [31:0] in_1,
  input  [4:0] in_2,
  output [31:0] out_3
);

  wire [4:0] subtractor_1_out;
  wire [31:0] adder_1_out, bit_extender_1_out, shifter_1_out, shifter_2_out, shifter_3_out;

  Shifter #(.width(32)) shifter_1 (.in(in_1), .\dist (5'b00001), .out(shifter_1_out));
  Adder #(.width(32)) adder_1 (.a(shifter_1_out), .b(32'h1), .out(adder_1_out));  // open: cin, cout
  Subtractor #(.width(5)) subtractor_1 (.a(5'b11010), .b(in_2), .out(subtractor_1_out));  // open: bin, bout
  Shifter #(.width(32)) shifter_2 (.in(adder_1_out), .\dist (subtractor_1_out), .out(shifter_2_out));
  Shifter #(.width(32)) shifter_3 (.in(shifter_2_out), .\dist (5'b00101), .out(shifter_3_out));
  assign out_3 = shifter_3_out | bit_extender_1_out;  // OR_Gate or_1, 32 bits wide
  assign bit_extender_1_out = {{27{1'b0}}, in_2};  // Bit_Extender bit_extender_1

  // Other names for the same wires on the sheet: input[31:0] = in_1; n[4:0] = in_2
endmodule
