// Logisim project calculate_score.circ as structural Verilog: 2 circuits, main circuit main
module main (
  input  [2:0] in_1,
  input  [1:0] in_2,
  input  [1:0] in_3,
  output [3:0] out_4
);

  wire comparator_1_eq;
  wire [3:0] bit_extender_1_out, bit_extender_2_out, bit_extender_3_out, sum3_1_out_4;

  assign bit_extender_1_out = {{2{1'b0}}, in_2};  // Bit_Extender bit_extender_1
  assign bit_extender_2_out = {{2{1'b0}}, in_3};  // Bit_Extender bit_extender_2
  assign bit_extender_3_out = {{1{1'b0}}, in_1};  // Bit_Extender bit_extender_3
  sum3 sum3_1 (.in_1(bit_extender_1_out), .in_2(bit_extender_2_out), .in_3(bit_extender_3_out), .out_4(sum3_1_out_4));
  Multiplexer #(.width(4), .enable("false")) multiplexer_1 (
    .in0(sum3_1_out_4), .in1(4'b0000), .out(out_4), .sel(comparator_1_eq));
  Comparator #(.width(3), .mode("unsigned")) comparator_1 (.a(in_1), .b(3'b000), .eq(comparator_1_eq));  // open: gt, lt

  // Other names for the same wires on the sheet: s1[1:0] = in_2; s2[1:0] = in_3; tea[2:0] = in_1; total[3:0] = out_4
endmodule

module sum3 (
  input  [3:0] in_1,
  input  [3:0] in_2,
  input  [3:0] in_3,
  output [3:0] out_4
);

  wire [3:0] adder_1_out;

  Adder #(.width(4)) adder_1 (.a(in_1), .b(in_2), .out(adder_1_out));  // open: cin, cout
  Adder #(.width(4)) adder_2 (.a(adder_1_out), .b(in_3), .out(out_4));  // open: cin, cout
endmodule
