// Logisim project shuffle_bus.circ as structural Verilog: 2 circuits, main circuit main
module main (
  input  in_1,
  input  in_2,
  input  in_3,
  output [1:0] out_4
);

  wire comparator_1_eq, multiplexer_1_out, new_line, register_1_q;
  wire [1:0] multiplexer_4_out, next_station, now_station;

  Multiplexer #(.enable("false")) multiplexer_1 (.in0(in_3), .in1(1'b0), .out(multiplexer_1_out), .sel(in_2));
  Register #(.width(1)) register_1 (.D(multiplexer_1_out), .en(new_line), .Q(register_1_q), .clk(in_1));  // open: clr
  Comparator #(.width(2), .mode("unsigned")) comparator_1 (
    .a(now_station), .b(2'b10), .eq(comparator_1_eq));  // open: gt, lt
  Multiplexer #(.enable("false")) multiplexer_2 (.in0(register_1_q), .in1(in_3), .out(new_line), .sel(comparator_1_eq));
  Multiplexer #(.width(2), .enable("false")) multiplexer_3 (.in0(next_station), .in1(2'b11), .out(out_4), .sel(in_2));
  route route_1 (.in_1(now_station), .in_2(new_line), .out_3(next_station));
  Multiplexer #(.width(2), .enable("false")) multiplexer_4 (
    .in0(next_station), .in1(2'b00), .out(multiplexer_4_out), .sel(in_2));
  Register #(.width(2)) register_2 (.D(multiplexer_4_out), .Q(now_station), .clk(in_1));  // open: en, clr

  // Other names for the same wires on the sheet: clk = in_1; line = in_3; out[1:0] = out_4; reset = in_2
endmodule

module route (
  input  [1:0] in_1,
  input  in_2,
  output [1:0] out_3
);

  wire [1:0] multiplexer_1_out, multiplexer_2_out;

  Multiplexer #(.select(2), .width(2), .enable("false")) multiplexer_1 (
    .in0(2'b11), .in1(2'b10), .in2(2'b00), .in3(2'b01), .out(multiplexer_1_out), .sel(in_1));
  Multiplexer #(.select(2), .width(2), .enable("false")) multiplexer_2 (
    .in1(2'b10), .in2(2'b11), .in3(2'b01), .out(multiplexer_2_out), .sel(in_1));  // open: in0
  Multiplexer #(.width(2), .enable("false")) multiplexer_3 (
    .in0(multiplexer_1_out), .in1(multiplexer_2_out), .out(out_3), .sel(in_2));

  // Other names for the same wires on the sheet: next_station[1:0] = out_3; now_station[1:0] = in_1; route = in_2
endmodule
