// Logisim project recurrence_array.circ as structural Verilog: 2 circuits, main circuit main
module main (
  input  in_1,
  input  [4:0] in_2,
  output [31:0] out_3
);

  wire _4, comparator_2_eq, enable, not_1_out, not_2_out, not_3_out, not_4_out, not_5_out, reset;
  wire [4:0] adder_2_out, n_q, subtractor_1_out;
  wire [31:0] a_n, a_n_1, a_n_1_q, a_n_2, a_n_2_q, a_n_3, a_n_3_q, and_1_out, controlled_buffer_1_out,
       n3_1_out_2, xor_1_out, xor_2_out, xor_3_out;

  Button button_1 (.out(reset));
  assign and_1_out = a_n_2 & a_n_3;  // AND_Gate and_1, 32 bits wide
  // Probe on and_1_out
  // Probe on a_n_1
  Adder #(.width(32)) adder_1 (.a(a_n_1), .b(and_1_out), .out(a_n));  // open: cin, cout
  assign xor_1_out = 32'h1 ^ a_n;  // XOR_Gate xor_1, 32 bits wide
  not not_1 (not_1_out, enable);
  assign xor_2_out = 32'h1 ^ a_n_1;  // XOR_Gate xor_2, 32 bits wide
  not not_2 (not_2_out, enable);
  assign xor_3_out = 32'h1 ^ a_n_2;  // XOR_Gate xor_3, 32 bits wide
  not not_3 (not_3_out, enable);
  Register #(.width(32)) u_a_n_1 (.D(xor_1_out), .en(not_1_out), .Q(a_n_1_q), .clk(in_1), .clr(reset));
  Register #(.width(32)) u_a_n_2 (.D(xor_2_out), .en(not_2_out), .Q(a_n_2_q), .clk(in_1), .clr(reset));
  Register #(.width(32)) u_a_n_3 (.D(xor_3_out), .en(not_3_out), .Q(a_n_3_q), .clk(in_1), .clr(reset));
  assign a_n_1 = 32'h1 ^ a_n_1_q;  // XOR_Gate xor_4, 32 bits wide
  assign a_n_2 = 32'h1 ^ a_n_2_q;  // XOR_Gate xor_5, 32 bits wide
  assign a_n_3 = 32'h1 ^ a_n_3_q;  // XOR_Gate xor_6, 32 bits wide
  Adder #(.width(5)) adder_2 (.a(n_q), .b(5'b00001), .out(adder_2_out));  // open: cin, cout
  assign controlled_buffer_1_out = not_4_out ? a_n_1 : 32'bz;  // Controlled_Buffer controlled_buffer_1
  not not_4 (not_4_out, _4);
  assign controlled_buffer_1_out = _4 ? n3_1_out_2 : 32'bz;  // Controlled_Buffer controlled_buffer_2
  _3 u_3_1 (.in_1(in_2), .out_2(n3_1_out_2));
  Register #(.width(5)) n (.D(adder_2_out), .en(not_5_out), .Q(n_q), .clk(in_1), .clr(reset));
  not not_5 (not_5_out, enable);
  Comparator #(.width(5), .mode("unsigned")) comparator_1 (.a(5'b00100), .b(in_2), .gt(_4));  // open: eq, lt
  Subtractor #(.width(5)) subtractor_1 (.a(in_2), .b(5'b00011), .out(subtractor_1_out));  // open: bin, bout
  Multiplexer #(.width(32), .enable("false")) multiplexer_1 (
    .in0({32{1'b0}}), .in1(controlled_buffer_1_out), .out(out_3), .sel(enable));
  Comparator #(.width(5), .mode("unsigned")) comparator_2 (
    .a(n_q), .b(subtractor_1_out), .eq(comparator_2_eq));  // open: gt, lt
  or or_1 (enable, _4, comparator_2_eq);
  // AND_Gate and_2 is placed but not wired

  // Other names for the same wires on the sheet: clk = in_1; N[4:0] = in_2; Nth[31:0] = out_3
endmodule

module _3 (
  input  [4:0] in_1,
  output [31:0] out_2
);

  wire [1:0] bit_extender_1_out;

  Multiplexer #(.select(2), .width(32), .enable("false")) multiplexer_1 (
    .in0({32{1'b0}}), .in1(32'h1), .in2(32'h1), .in3(32'h1), .out(out_2), .sel(bit_extender_1_out));
  Bit_Extender #(.in_width(5), .out_width(2)) bit_extender_1 (.in(in_1), .out(bit_extender_1_out));
endmodule
