// Logisim project fibonacci_modification.circ as structural Verilog: 2 circuits, main circuit main
module main (
  input  in_1,
  input  in_2,
  input  [4:0] in_3,
  output [31:0] out_4
);

  wire _3, bitselector_1_out, comparator_1_eq, comparator_1_gt, comparator_2_eq, enable, not_1_out,
       not_2_out, not_3_out, not_4_out, not_5_out;
  wire [4:0] adder_3_out, divider_1_rem, n, subtractor_1_out;
  wire [31:0] adder_1_out, adder_2_out, controlled_buffer_1_out, n3_1_out_2, s_n, s_n_1, s_n_2, s_n_2_q,
       s_n_input, s_n_q, xor_1_out, xor_2_out, xor_3_out, xor_4_out;

  // Probe on adder_1_out
  assign xor_1_out = s_n_1 ^ s_n_2;  // XOR_Gate xor_1, 32 bits wide
  Adder #(.width(32)) adder_1 (.a(xor_1_out), .b(s_n), .out(adder_1_out));  // open: cin, cout
  assign xor_2_out = s_n_1 ^ s_n;  // XOR_Gate xor_2, 32 bits wide
  Adder #(.width(32)) adder_2 (.a(xor_2_out), .b(s_n_2), .out(adder_2_out));  // open: cin, cout
  Divider #(.width(5)) divider_1 (.a(n), .b(5'b00010), .rem(divider_1_rem));  // open: out, upper
  // Probe on xor_1_out
  Multiplexer #(.width(32), .enable("false")) multiplexer_1 (
    .in0(adder_1_out), .in1(adder_2_out), .out(s_n_input), .sel(bitselector_1_out));
  BitSelector #(.width(5)) bitselector_1 (.in(divider_1_rem), .out(bitselector_1_out), .sel(3'b000));
  assign xor_3_out = 32'h1 ^ s_n_input;  // XOR_Gate xor_3, 32 bits wide
  assign xor_4_out = 32'h1 ^ s_n_1;  // XOR_Gate xor_4, 32 bits wide
  // Probe on adder_2_out
  not not_1 (not_1_out, enable);
  not not_2 (not_2_out, enable);
  not not_3 (not_3_out, enable);
  assign s_n = 32'h1 ^ s_n_q;  // XOR_Gate xor_5, 32 bits wide
  Register #(.width(32)) u_s_n (.D(xor_3_out), .en(not_1_out), .Q(s_n_q), .clk(in_1), .clr(in_2));
  Register #(.width(32)) u_s_n_1 (.D(s_n), .en(not_2_out), .Q(s_n_1), .clk(in_1), .clr(in_2));
  assign s_n_2 = 32'h1 ^ s_n_2_q;  // XOR_Gate xor_6, 32 bits wide
  Register #(.width(32)) u_s_n_2 (.D(xor_4_out), .en(not_3_out), .Q(s_n_2_q), .clk(in_1), .clr(in_2));
  // Probe on s_n_1
  Adder #(.width(5)) adder_3 (.a(n), .b(5'b00001), .out(adder_3_out));  // open: cin, cout
  Comparator #(.width(5), .mode("unsigned")) comparator_1 (
    .a(5'b00011), .b(in_3), .gt(comparator_1_gt), .eq(comparator_1_eq));  // open: lt
  Register #(.width(5)) register_1 (.D(adder_3_out), .en(not_4_out), .Q(n), .clk(in_1), .clr(in_2));
  not not_4 (not_4_out, enable);
  assign controlled_buffer_1_out = not_5_out ? s_n : 32'bz;  // Controlled_Buffer controlled_buffer_1
  not not_5 (not_5_out, _3);
  assign controlled_buffer_1_out = _3 ? n3_1_out_2 : 32'bz;  // Controlled_Buffer controlled_buffer_2
  _3 u_3_1 (.in_1(in_3), .out_2(n3_1_out_2));
  or or_1 (_3, comparator_1_gt, comparator_1_eq);
  Subtractor #(.width(5)) subtractor_1 (.a(in_3), .b(5'b00011), .out(subtractor_1_out));  // open: bin, bout
  // Probe on s_n_2
  Comparator #(.width(5), .mode("unsigned")) comparator_2 (
    .a(n), .b(subtractor_1_out), .eq(comparator_2_eq));  // open: gt, lt
  Multiplexer #(.width(32), .enable("false")) multiplexer_2 (
    .in0(controlled_buffer_1_out), .in1({32{1'b0}}), .out(out_4), .sel(in_2));
  or or_2 (enable, _3, comparator_2_eq);

  // Other names for the same wires on the sheet: clk = in_1; in[4:0] = in_3; out[31:0] = out_4; rst = in_2
endmodule

module _3 (
  input  [4:0] in_1,
  output [31:0] out_2
);

  wire [4:0] divider_1_rem;

  Divider #(.width(5)) divider_1 (.a(in_1), .b(5'b00010), .rem(divider_1_rem));  // open: out, upper
  assign out_2 = {{27{1'b0}}, divider_1_rem};  // Bit_Extender bit_extender_1
endmodule
