// Logisim project text_match.circ as structural Verilog: 3 circuits, main circuit main
module main (
  input  in_1,
  input  in_2,
  input  [1:0] in_3,
  output [1:0] out_4
);

  wire enable, not_1_out;
  wire [1:0] adder_1_out, n0121_1_out_5, prev1, prev2, prev3, register_4_q;

  Adder #(.width(2)) adder_1 (.a(register_4_q), .b(2'b01), .out(adder_1_out));  // open: cin, cout
  Register #(.width(2)) register_1 (.D(in_3), .Q(prev1), .clk(in_1), .clr(in_2));  // open: en
  Register #(.width(2)) register_2 (.D(prev1), .Q(prev2), .clk(in_1), .clr(in_2));  // open: en
  Register #(.width(2)) register_3 (.D(prev2), .Q(prev3), .clk(in_1), .clr(in_2));  // open: en
  Register #(.width(2)) register_4 (.D(adder_1_out), .en(not_1_out), .Q(register_4_q), .clk(in_1), .clr(in_2));
  not not_1 (not_1_out, enable);
  Comparator #(.width(2), .mode("unsigned")) comparator_1 (.a(register_4_q), .b(2'b11), .eq(enable));  // open: gt, lt
  _0121 u_0121_1 (.in_1(in_3), .in_2(prev1), .in_3(prev2), .in_4(prev3), .out_5(n0121_1_out_5[0]));
  _1210 u_1210_1 (.in_1(in_3), .in_2(prev1), .in_3(prev2), .in_4(prev3), .out_5(n0121_1_out_5[1]));
  Multiplexer #(.width(2), .enable("false")) multiplexer_1 (
    .in0(2'b00), .in1(n0121_1_out_5), .out(out_4), .sel(enable));

  // Other names for the same wires on the sheet: clk = in_1; in[1:0] = in_3; out[1:0] = out_4; rst = in_2
endmodule

module _0121 (
  input  [1:0] in_1,
  input  [1:0] in_2,
  input  [1:0] in_3,
  input  [1:0] in_4,
  output out_5
);

  wire comparator_1_eq, comparator_2_eq, comparator_3_eq, comparator_4_eq;

  Comparator #(.width(2), .mode("unsigned")) comparator_1 (.a(in_1), .b(2'b01), .eq(comparator_1_eq));  // open: gt, lt
  Comparator #(.width(2), .mode("unsigned")) comparator_2 (.a(in_2), .b(2'b10), .eq(comparator_2_eq));  // open: gt, lt
  Comparator #(.width(2), .mode("unsigned")) comparator_3 (.a(in_3), .b(2'b01), .eq(comparator_3_eq));  // open: gt, lt
  Comparator #(.width(2), .mode("unsigned")) comparator_4 (.a(in_4), .b(2'b00), .eq(comparator_4_eq));  // open: gt, lt
  and and_1 (out_5, comparator_1_eq, comparator_2_eq, comparator_3_eq, comparator_4_eq);
endmodule

module _1210 (
  input  [1:0] in_1,
  input  [1:0] in_2,
  input  [1:0] in_3,
  input  [1:0] in_4,
  output out_5
);

  wire comparator_1_eq, comparator_2_eq, comparator_3_eq, comparator_4_eq;

  Comparator #(.width(2), .mode("unsigned")) comparator_1 (.a(in_1), .b(2'b00), .eq(comparator_1_eq));  // open: gt, lt
  Comparator #(.width(2), .mode("unsigned")) comparator_2 (.a(in_2), .b(2'b01), .eq(comparator_2_eq));  // open: gt, lt
  Comparator #(.width(2), .mode("unsigned")) comparator_3 (.a(in_3), .b(2'b10), .eq(comparator_3_eq));  // open: gt, lt
  Comparator #(.width(2), .mode("unsigned")) comparator_4 (.a(in_4), .b(2'b01), .eq(comparator_4_eq));  // open: gt, lt
  and and_1 (out_5, comparator_1_eq, comparator_2_eq, comparator_3_eq, comparator_4_eq);
endmodule
