// Logisim project vote.circ as structural Verilog: 2 circuits, main circuit main
module main (
  input  [1:0] in_1,
  input  [1:0] in_2,
  input  [1:0] in_3,
  input  [1:0] in_4,
  input  [1:0] in_5,
  input  [1:0] in_6,
  output out_7
);

  wire decoder_1_out0, decoder_1_out1, decoder_1_out2, decoder_1_out3, equal, not_1_out, not_2_out,
       not_3_out, not_4_out, T0En, T1En, T2En, T3En;
  wire [1:0] LVout, multiplexer_1_out, multiplexer_2_out, multiplexer_3_out, multiplexer_4_out,
       multiplexer_5_out, T0out, T1out, T2out, T3out;
  wire [3:0] sum5_1_out_6;

  Multiplexer #(.select(2), .width(2), .enable("false")) multiplexer_1 (
    .in0(2'b01), .in1(2'b11), .in2(2'b00), .in3(2'b10), .out(multiplexer_1_out), .sel(in_1));
  Multiplexer #(.select(2), .width(2), .enable("false")) multiplexer_2 (
    .in0(2'b01), .in1(2'b11), .in2(2'b00), .in3(2'b11), .out(multiplexer_2_out), .sel(in_3));
  not not_1 (not_1_out, T0En);
  Multiplexer #(.select(2), .width(2), .enable("false")) multiplexer_3 (
    .in0(2'b01), .in1(2'b11), .in2(2'b00), .in3(2'b11), .out(multiplexer_3_out), .sel(in_4));
  not not_2 (not_2_out, T1En);
  Multiplexer #(.select(2), .width(2), .enable("false")) multiplexer_4 (
    .in0(2'b01), .in1(2'b11), .in2(2'b00), .in3(2'b11), .out(multiplexer_4_out), .sel(in_5));
  not not_3 (not_3_out, T2En);
  Multiplexer #(.select(2), .width(2), .enable("false")) multiplexer_5 (
    .in0(2'b01), .in1(2'b11), .in2(2'b00), .in3(2'b11), .out(multiplexer_5_out), .sel(in_6));
  not not_4 (not_4_out, T3En);
  Comparator #(.width(2), .mode("unsigned")) comparator_1 (
    .a(multiplexer_1_out), .b(2'b10), .eq(equal));  // open: gt, lt
  // Probe on T0out
  assign T0out = not_1_out ? multiplexer_2_out : 2'bz;  // Controlled_Buffer controlled_buffer_1
  assign T0out = T0En ? 2'b00 : 2'bz;  // Controlled_Buffer controlled_buffer_2
  assign T1out = not_2_out ? multiplexer_3_out : 2'bz;  // Controlled_Buffer controlled_buffer_3
  assign T1out = T1En ? 2'b00 : 2'bz;  // Controlled_Buffer controlled_buffer_4
  assign T2out = not_3_out ? multiplexer_4_out : 2'bz;  // Controlled_Buffer controlled_buffer_5
  assign T2out = T2En ? 2'b00 : 2'bz;  // Controlled_Buffer controlled_buffer_6
  assign T3out = not_4_out ? multiplexer_5_out : 2'bz;  // Controlled_Buffer controlled_buffer_7
  assign T3out = T3En ? 2'b00 : 2'bz;  // Controlled_Buffer controlled_buffer_8
  Multiplexer #(.width(2), .enable("false")) multiplexer_6 (
    .in0(multiplexer_1_out), .in1(2'b00), .out(LVout), .sel(equal));
  Decoder #(.select(2), .enable("false")) decoder_1 (
    .out0(decoder_1_out0), .out1(decoder_1_out1), .out2(decoder_1_out2), .out3(decoder_1_out3), .sel(in_2));
  Multiplexer #(.enable("false")) multiplexer_7 (.in0(1'b0), .in1(decoder_1_out0), .out(T0En), .sel(equal));
  Multiplexer #(.enable("false")) multiplexer_8 (.in0(1'b0), .in1(decoder_1_out1), .out(T1En), .sel(equal));
  Multiplexer #(.enable("false")) multiplexer_9 (.in0(1'b0), .in1(decoder_1_out2), .out(T2En), .sel(equal));
  Multiplexer #(.enable("false")) multiplexer_10 (.in0(1'b0), .in1(decoder_1_out3), .out(T3En), .sel(equal));
  // Probe on sum5_1_out_6
  sum5 sum5_1 (.in_1(LVout), .in_2(T0out), .in_3(T1out), .in_4(T2out), .in_5(T3out), .out_6(sum5_1_out_6));
  Comparator #(.width(4)) comparator_2 (.a(sum5_1_out_6), .b(4'b0000), .gt(out_7));  // open: eq, lt

  // Other names for the same wires on the sheet: LI[1:0] = in_2; LV[1:0] = in_1; O = out_7; T0[1:0] = in_3;
  //   T1[1:0] = in_4; T2[1:0] = in_5; T3[1:0] = in_6
endmodule

module sum5 (
  input  [1:0] in_1,
  input  [1:0] in_2,
  input  [1:0] in_3,
  input  [1:0] in_4,
  input  [1:0] in_5,
  output [3:0] out_6
);

  wire [3:0] adder_1_out, adder_2_out, adder_3_out, bit_extender_1_out, bit_extender_2_out,
       bit_extender_3_out, bit_extender_4_out, bit_extender_5_out;

  assign bit_extender_1_out = {{2{in_1[1]}}, in_1};  // Bit_Extender bit_extender_1
  assign bit_extender_2_out = {{2{in_2[1]}}, in_2};  // Bit_Extender bit_extender_2
  assign bit_extender_3_out = {{2{in_3[1]}}, in_3};  // Bit_Extender bit_extender_3
  assign bit_extender_4_out = {{2{in_4[1]}}, in_4};  // Bit_Extender bit_extender_4
  assign bit_extender_5_out = {{2{in_5[1]}}, in_5};  // Bit_Extender bit_extender_5
  Adder #(.width(4)) adder_1 (.a(bit_extender_1_out), .b(bit_extender_2_out), .out(adder_1_out));  // open: cin, cout
  Adder #(.width(4)) adder_2 (.a(bit_extender_3_out), .b(bit_extender_4_out), .out(adder_2_out));  // open: cin, cout
  Adder #(.width(4)) adder_3 (.a(adder_2_out), .b(bit_extender_5_out), .out(adder_3_out));  // open: cin, cout
  Adder #(.width(4)) adder_4 (.a(adder_1_out), .b(adder_3_out), .out(out_6));  // open: cin, cout
endmodule
