// Logisim project hexdecimal_match.circ as structural Verilog: 2 circuits, main circuit main
module main (
  input  [3:0] in_1,
  input  in_2,
  input  in_3,
  output [1:0] out_4
);

  wire comparator_1_eq, enable;
  wire [1:0] judge_1_out_4;
  wire [3:0] adder_1_out, buffer1, buffer2, buffer3, check_q;

  Adder #(.width(4)) adder_1 (.a(check_q), .b(4'b0001), .out(adder_1_out));  // open: cin, cout
  Register #(.width(4)) now (.D(in_1), .Q(buffer1), .clk(in_2), .clr(in_3));  // open: en
  Register #(.width(4)) prev1 (.D(buffer1), .Q(buffer2), .clk(in_2), .clr(in_3));  // open: en
  Register #(.width(4)) prev2 (.D(buffer2), .Q(buffer3), .clk(in_2), .clr(in_3));  // open: en
  Register #(.width(4)) check (.D(adder_1_out), .en(enable), .Q(check_q), .clk(in_2), .clr(in_3));
  Comparator #(.width(4), .mode("unsigned")) comparator_1 (
    .a(check_q), .b(4'b0011), .eq(comparator_1_eq));  // open: gt, lt
  not not_1 (enable, comparator_1_eq);
  judge judge_1 (.in_1(buffer1), .in_2(buffer2), .in_3(buffer3), .out_4(judge_1_out_4));
  Multiplexer #(.width(2), .enable("false")) multiplexer_1 (
    .in0(judge_1_out_4), .in1(2'b00), .out(out_4), .sel(enable));

  // Other names for the same wires on the sheet: clk = in_2; input[3:0] = in_1; output[1:0] = out_4; reset = in_3
endmodule

module judge (
  input  [3:0] in_1,
  input  [3:0] in_2,
  input  [3:0] in_3,
  output [1:0] out_4
);

  wire comparator_1_eq, comparator_2_eq, comparator_3_eq, comparator_4_eq, comparator_5_eq, comparator_6_eq,
       comparator_7_eq, comparator_8_eq, comparator_9_eq;
  wire [2:0] and_1_out;

  Comparator #(.width(4), .mode("unsigned")) comparator_1 (
    .a(in_1), .b(4'b1110), .eq(comparator_1_eq));  // open: gt, lt
  Comparator #(.width(4), .mode("unsigned")) comparator_2 (
    .a(in_2), .b(4'b0000), .eq(comparator_2_eq));  // open: gt, lt
  Comparator #(.width(4), .mode("unsigned")) comparator_3 (
    .a(in_3), .b(4'b1010), .eq(comparator_3_eq));  // open: gt, lt
  Comparator #(.width(4), .mode("unsigned")) comparator_4 (
    .a(in_1), .b(4'b1110), .eq(comparator_4_eq));  // open: gt, lt
  Comparator #(.width(4), .mode("unsigned")) comparator_5 (
    .a(in_2), .b(4'b1110), .eq(comparator_5_eq));  // open: gt, lt
  Comparator #(.width(4), .mode("unsigned")) comparator_6 (
    .a(in_3), .b(4'b1110), .eq(comparator_6_eq));  // open: gt, lt
  Comparator #(.width(4), .mode("unsigned")) comparator_7 (
    .a(in_1), .b(4'b0000), .eq(comparator_7_eq));  // open: gt, lt
  Comparator #(.width(4), .mode("unsigned")) comparator_8 (
    .a(in_2), .b(4'b1010), .eq(comparator_8_eq));  // open: gt, lt
  Comparator #(.width(4), .mode("unsigned")) comparator_9 (
    .a(in_3), .b(4'b0000), .eq(comparator_9_eq));  // open: gt, lt
  and and_1 (and_1_out[0], comparator_1_eq, comparator_2_eq, comparator_3_eq);
  and and_2 (and_1_out[1], comparator_4_eq, comparator_5_eq, comparator_6_eq);
  and and_3 (and_1_out[2], comparator_7_eq, comparator_8_eq, comparator_9_eq);
  Multiplexer #(.select(3), .width(2), .enable("false")) multiplexer_1 (
    .in0(2'b00), .in1(2'b01), .in2(2'b10), .in4(2'b11), .out(out_4), .sel(and_1_out));  // open: in3, in5, in6, in7

  // Other names for the same wires on the sheet: input1[3:0] = in_1; input2[3:0] = in_2; input3[3:0] = in_3
endmodule
