// Logisim project nonexist.circ as structural Verilog: 2 circuits, main circuit main
module main (
  input  [7:0] in_1,
  input  [7:0] in_2,
  input  [7:0] in_3,
  input  [7:0] in_4,
  input  [7:0] in_5,
  output [7:0] out_6
);

  wire [2:0] bitfinder_1_index;
  wire [4:0] is_exist_1_out_7;
  wire [7:0] bit_extender_1_out;

  is_exist is_exist_1 (
    .in_1(in_1), .in_2(in_2), .in_3(in_3), .in_4(in_4), .in_5(in_5), .in_6(8'h1), .out_7(is_exist_1_out_7[0]));
  is_exist is_exist_2 (
    .in_1(in_1), .in_2(in_2), .in_3(in_3), .in_4(in_4), .in_5(in_5), .in_6(8'h2), .out_7(is_exist_1_out_7[1]));
  is_exist is_exist_3 (
    .in_1(in_1), .in_2(in_2), .in_3(in_3), .in_4(in_4), .in_5(in_5), .in_6(8'h3), .out_7(is_exist_1_out_7[2]));
  is_exist is_exist_4 (
    .in_1(in_1), .in_2(in_2), .in_3(in_3), .in_4(in_4), .in_5(in_5), .in_6(8'h4), .out_7(is_exist_1_out_7[3]));
  is_exist is_exist_5 (
    .in_1(in_1), .in_2(in_2), .in_3(in_3), .in_4(in_4), .in_5(in_5), .in_6(8'h5), .out_7(is_exist_1_out_7[4]));
  BitFinder #(.width(6), .\type ("low0")) bitfinder_1 (
    .in({1'b0, is_exist_1_out_7}), .index(bitfinder_1_index));  // open: found
  // Probe on bit_extender_1_out
  assign bit_extender_1_out = {{5{1'b0}}, bitfinder_1_index};  // Bit_Extender bit_extender_1
  Adder adder_1 (.a(bit_extender_1_out), .b(8'h1), .out(out_6));  // open: cin, cout

  // Other names for the same wires on the sheet: input1[7:0] = in_1; input2[7:0] = in_2; input3[7:0] = in_3;
  //   input4[7:0] = in_4; input5[7:0] = in_5; output[7:0] = out_6
endmodule

module is_exist (
  input  [7:0] in_1,
  input  [7:0] in_2,
  input  [7:0] in_3,
  input  [7:0] in_4,
  input  [7:0] in_5,
  input  [7:0] in_6,
  output out_7
);

  wire comparator_1_eq, comparator_2_eq, comparator_3_eq, comparator_4_eq, comparator_5_eq;

  Comparator comparator_1 (.a(in_1), .b(in_6), .eq(comparator_1_eq));  // open: gt, lt
  Comparator comparator_2 (.a(in_2), .b(in_6), .eq(comparator_2_eq));  // open: gt, lt
  Comparator comparator_3 (.a(in_3), .b(in_6), .eq(comparator_3_eq));  // open: gt, lt
  Comparator comparator_4 (.a(in_4), .b(in_6), .eq(comparator_4_eq));  // open: gt, lt
  Comparator comparator_5 (.a(in_5), .b(in_6), .eq(comparator_5_eq));  // open: gt, lt
  or or_1 (out_7, comparator_1_eq, comparator_2_eq, comparator_3_eq, comparator_4_eq, comparator_5_eq);

  // Other names for the same wires on the sheet: input1[7:0] = in_1; input2[7:0] = in_2; input3[7:0] = in_3;
  //   input4[7:0] = in_4; input5[7:0] = in_5; standard[7:0] = in_6
endmodule
