// Logisim project wander.circ as structural Verilog: 3 circuits, main circuit main
module main (
  input  [1:0] in_1,
  input  in_2,
  input  in_3,
  output [3:0] out_4
);

  wire down, enable, left, right, up, wall_1_out_3;
  wire [2:0] adder_1_out, adder_2_out, bufferx, buffery, multiplexer_1_out, multiplexer_2_out,
       multiplexer_5_out, multiplexer_6_out, outputx, outputy, subtractor_1_out, subtractor_2_out;

  Decoder #(.select(2), .enable("false")) decoder_1 (.out0(up), .out1(down), .out2(left), .out3(right), .sel(in_1));
  Register #(.width(3)) x (.D(bufferx), .en(enable), .Q(outputx), .clk(in_3), .clr(in_2));
  Register #(.width(3)) y (.D(buffery), .en(enable), .Q(outputy), .clk(in_3), .clr(in_2));
  wall wall_1 (.in_1(bufferx), .in_2(buffery), .out_3(wall_1_out_3));
  not not_1 (enable, wall_1_out_3);
  Adder #(.width(3)) adder_1 (.a(outputx), .b(3'b001), .out(adder_1_out));  // open: cin, cout
  Adder #(.width(3)) adder_2 (.a(outputy), .b(3'b001), .out(adder_2_out));  // open: cin, cout
  Multiplexer #(.width(3), .enable("false")) multiplexer_1 (
    .in0(outputx), .in1(adder_1_out), .out(multiplexer_1_out), .sel(left));
  Multiplexer #(.width(3), .enable("false")) multiplexer_2 (
    .in0(outputy), .in1(adder_2_out), .out(multiplexer_2_out), .sel(down));
  Multiplexer #(.width(3), .enable("false")) multiplexer_3 (
    .in0(multiplexer_1_out), .in1(subtractor_1_out), .out(bufferx), .sel(right));
  Subtractor #(.width(3)) subtractor_1 (.a(multiplexer_1_out), .b(3'b001), .out(subtractor_1_out));  // open: bin, bout
  Multiplexer #(.width(3), .enable("false")) multiplexer_4 (
    .in0(multiplexer_2_out), .in1(subtractor_2_out), .out(buffery), .sel(up));
  Subtractor #(.width(3)) subtractor_2 (.a(multiplexer_2_out), .b(3'b001), .out(subtractor_2_out));  // open: bin, bout
  Multiplexer #(.width(3), .enable("false")) multiplexer_5 (
    .in0(outputx), .in1(bufferx), .out(multiplexer_5_out), .sel(enable));
  \output  output_1 (.in_1(multiplexer_5_out), .in_2(multiplexer_6_out), .out_3(out_4));
  Multiplexer #(.width(3), .enable("false")) multiplexer_6 (
    .in0(outputy), .in1(buffery), .out(multiplexer_6_out), .sel(enable));

  // Other names for the same wires on the sheet: clk = in_3; input[1:0] = in_1; output[3:0] = out_4; reset = in_2
endmodule

module wall (
  input  [2:0] in_1,
  input  [2:0] in_2,
  output out_3
);

  wire and_1_out, comparator_1_lt, comparator_2_lt, comparator_3_gt, comparator_4_gt, comparator_5_eq,
       comparator_6_eq;

  Comparator #(.width(3)) comparator_1 (.a(in_1), .b(3'b000), .lt(comparator_1_lt));  // open: gt, eq
  Comparator #(.width(3)) comparator_2 (.a(in_2), .b(3'b000), .lt(comparator_2_lt));  // open: gt, eq
  Comparator #(.width(3)) comparator_3 (.a(in_1), .b(3'b010), .gt(comparator_3_gt));  // open: eq, lt
  Comparator #(.width(3)) comparator_4 (.a(in_2), .b(3'b010), .gt(comparator_4_gt));  // open: eq, lt
  Comparator #(.width(3)) comparator_5 (.a(in_1), .b(3'b001), .eq(comparator_5_eq));  // open: gt, lt
  Comparator #(.width(3)) comparator_6 (.a(in_2), .b(3'b001), .eq(comparator_6_eq));  // open: gt, lt
  and and_1 (and_1_out, comparator_5_eq, comparator_6_eq);
  or or_1 (out_3, comparator_1_lt, comparator_2_lt, comparator_3_gt, comparator_4_gt, and_1_out);

  // Other names for the same wires on the sheet: x[2:0] = in_1; y[2:0] = in_2
endmodule

module \output  (
  input  [2:0] in_1,
  input  [2:0] in_2,
  output [3:0] out_3
);

  wire [3:0] adder_1_out, multiplier_1_out, subtractor_1_out, subtractor_2_out;

  Adder #(.width(4)) adder_1 (.a({1'b0, in_2}), .b(4'b0001), .out(adder_1_out));  // open: cin, cout
  Subtractor #(.width(4)) subtractor_1 (.a(4'b1000), .b(multiplier_1_out), .out(subtractor_1_out));  // open: bin, bout
  Multiplier #(.width(4)) multiplier_1 (.a({1'b0, in_2}), .b(4'b0010), .out(multiplier_1_out));  // open: cin, cout
  Subtractor #(.width(4)) subtractor_2 (.a(4'b0111), .b({1'b0, in_2}), .out(subtractor_2_out));  // open: bin, bout
  Multiplexer #(.select(2), .width(4), .enable("false")) multiplexer_1 (
    .in0(adder_1_out), .in1(subtractor_1_out), .in2(subtractor_2_out), .out(out_3), .sel(in_1[1:0]));  // open: in3

  // Other names for the same wires on the sheet: x[2:0] = in_1; y[2:0] = in_2
endmodule
