// Logisim project increasing_suffix.circ as structural Verilog: 1 circuit, main circuit main
module main (
  input  in_1,
  input  in_2,
  input  [3:0] in_3,
  output [4:0] out_4
);

  wire comparator_1_lt, comparator_2_eq, enable;
  wire [3:0] buffer1;
  wire [4:0] adder_1_out, multiplexer_2_out, multiplexer_3_out;

  Comparator #(.width(4), .mode("unsigned")) comparator_1 (
    .a(buffer1), .b(in_3), .lt(comparator_1_lt));  // open: gt, eq
  Comparator #(.width(5), .mode("unsigned")) comparator_2 (
    .a(out_4), .b({5{1'b0}}), .eq(comparator_2_eq));  // open: gt, lt
  Register #(.width(4)) prev_data (.D(in_3), .Q(buffer1), .clk(in_1));  // open: en, clr
  Multiplexer #(.enable("false")) multiplexer_1 (
    .in0(comparator_1_lt), .in1(1'b1), .out(enable), .sel(comparator_2_eq));
  Multiplexer #(.width(5), .enable("false")) multiplexer_2 (
    .in0(5'b00001), .in1(adder_1_out), .out(multiplexer_2_out), .sel(enable));
  Adder #(.width(5)) adder_1 (.a(out_4), .b(5'b00001), .out(adder_1_out));  // open: cin, cout
  Multiplexer #(.width(5), .enable("false")) multiplexer_3 (
    .in0(multiplexer_2_out), .in1({5{1'b0}}), .out(multiplexer_3_out), .sel(in_2));
  Register #(.width(5)) Length (.D(multiplexer_3_out), .Q(out_4), .clk(in_1));  // open: en, clr

  // Other names for the same wires on the sheet: clk = in_1; data[3:0] = in_3; length[4:0] = out_4; reset = in_2
endmodule
