// Logisim project inversion_pair.circ as structural Verilog: 2 circuits, main circuit main
module main (
  input  [1:0] in_1,
  input  [1:0] in_2,
  input  [1:0] in_3,
  input  [1:0] in_4,
  output [2:0] out_5
);

  wire comparator_1_gt, comparator_2_gt, comparator_3_gt, comparator_4_gt, comparator_5_gt, comparator_6_gt;
  wire [2:0] bit_extender_1_out, bit_extender_2_out, bit_extender_3_out, bit_extender_4_out,
       bit_extender_5_out, bit_extender_6_out;

  Comparator #(.width(2), .mode("unsigned")) comparator_1 (.a(in_1), .b(in_2), .gt(comparator_1_gt));  // open: eq, lt
  Comparator #(.width(2), .mode("unsigned")) comparator_2 (.a(in_1), .b(in_3), .gt(comparator_2_gt));  // open: eq, lt
  Comparator #(.width(2), .mode("unsigned")) comparator_3 (.a(in_1), .b(in_4), .gt(comparator_3_gt));  // open: eq, lt
  Comparator #(.width(2), .mode("unsigned")) comparator_4 (.a(in_2), .b(in_3), .gt(comparator_4_gt));  // open: eq, lt
  Comparator #(.width(2), .mode("unsigned")) comparator_5 (.a(in_2), .b(in_4), .gt(comparator_5_gt));  // open: eq, lt
  Comparator #(.width(2), .mode("unsigned")) comparator_6 (.a(in_3), .b(in_4), .gt(comparator_6_gt));  // open: eq, lt
  assign bit_extender_1_out = {{2{1'b0}}, comparator_1_gt};  // Bit_Extender bit_extender_1
  assign bit_extender_2_out = {{2{1'b0}}, comparator_2_gt};  // Bit_Extender bit_extender_2
  assign bit_extender_3_out = {{2{1'b0}}, comparator_3_gt};  // Bit_Extender bit_extender_3
  assign bit_extender_4_out = {{2{1'b0}}, comparator_4_gt};  // Bit_Extender bit_extender_4
  assign bit_extender_5_out = {{2{1'b0}}, comparator_5_gt};  // Bit_Extender bit_extender_5
  assign bit_extender_6_out = {{2{1'b0}}, comparator_6_gt};  // Bit_Extender bit_extender_6
  sum6 sum6_1 (
    .in_1(bit_extender_1_out), .in_2(bit_extender_2_out), .in_3(bit_extender_3_out),
    .in_4(bit_extender_4_out), .in_5(bit_extender_5_out), .in_6(bit_extender_6_out), .out_7(out_5));

  // Other names for the same wires on the sheet: a0[1:0] = in_1; a1[1:0] = in_2; a2[1:0] = in_3; a3[1:0] = in_4;
  //   count[2:0] = out_5
endmodule

module sum6 (
  input  [2:0] in_1,
  input  [2:0] in_2,
  input  [2:0] in_3,
  input  [2:0] in_4,
  input  [2:0] in_5,
  input  [2:0] in_6,
  output [2:0] out_7
);

  wire [2:0] adder_1_out, adder_2_out, adder_3_out, adder_4_out;

  Adder #(.width(3)) adder_1 (.a(in_1), .b(in_2), .out(adder_1_out));  // open: cin, cout
  Adder #(.width(3)) adder_2 (.a(in_3), .b(in_4), .out(adder_2_out));  // open: cin, cout
  Adder #(.width(3)) adder_3 (.a(in_5), .b(in_6), .out(adder_3_out));  // open: cin, cout
  Adder #(.width(3)) adder_4 (.a(adder_1_out), .b(adder_2_out), .out(adder_4_out));  // open: cin, cout
  Adder #(.width(3)) adder_5 (.a(adder_4_out), .b(adder_3_out), .out(out_7));  // open: cin, cout
endmodule
