// Logisim project study_room.circ as structural Verilog: 1 circuit, main circuit main
module main (
  input  in_1,
  input  in_2,
  input  [1:0] in_3,
  output [31:0] out_4
);

  wire decoder_1_out0, decoder_1_out1;
  wire [31:0] adder_1_out, adder_2_out, buffer0, buffer1, input0, input1, subtractor_1_out, subtractor_2_out;

  Decoder #(.enable("false")) decoder_1 (.out0(decoder_1_out0), .out1(decoder_1_out1), .sel(in_2));
  Adder #(.width(32)) adder_1 (.a(buffer0), .b(32'h1), .out(adder_1_out));  // open: cin, cout
  Adder #(.width(32)) adder_2 (.a(buffer1), .b(32'h1), .out(adder_2_out));  // open: cin, cout
  Register #(.width(32)) room_0 (.D(input0), .en(decoder_1_out0), .Q(buffer0), .clk(in_1));  // open: clr
  Register #(.width(32)) room_1 (.D(input1), .en(decoder_1_out1), .Q(buffer1), .clk(in_1));  // open: clr
  Adder #(.width(32)) adder_3 (.a(buffer0), .b(buffer1), .out(out_4));  // open: cin, cout
  Subtractor #(.width(32)) subtractor_1 (.a(buffer0), .b(32'h1), .out(subtractor_1_out));  // open: bin, bout
  Subtractor #(.width(32)) subtractor_2 (.a(buffer1), .b(32'h1), .out(subtractor_2_out));  // open: bin, bout
  Multiplexer #(.select(2), .width(32), .enable("false")) multiplexer_1 (
    .in0(buffer0), .in1(adder_1_out), .in2(subtractor_1_out), .in3({32{1'b0}}), .out(input0), .sel(in_3));
  Multiplexer #(.select(2), .width(32), .enable("false")) multiplexer_2 (
    .in0(buffer1), .in1(adder_2_out), .in2(subtractor_2_out), .in3({32{1'b0}}), .out(input1), .sel(in_3));

  // Other names for the same wires on the sheet: clk = in_1; op[1:0] = in_3; room = in_2; total[31:0] = out_4
endmodule
