// Logisim project binary_calculator.circ as structural Verilog: 1 circuit, main circuit main
module main (
  input  [1:0] in_1,
  input  [7:0] in_2,
  input  in_3,
  output [7:0] out_4
);

  wire [7:0] _01, _10, _11, result, shifter_1_out, shifter_2_out, shifter_3_out;

  Multiplexer #(.select(2), .width(8), .enable("false")) multiplexer_1 (
    .in0({8{1'b0}}), .in1(_01), .in2(_10), .in3(_11), .out(out_4), .sel(in_1));
  Register register_1 (.D(out_4), .Q(result), .clk(in_3));  // open: en, clr
  Shifter shifter_1 (.in(result), .\dist (3'b001), .out(shifter_1_out));
  Shifter shifter_2 (.in(result), .\dist (3'b001), .out(shifter_2_out));
  Shifter shifter_3 (.in(result), .\dist (3'b001), .out(shifter_3_out));
  Adder adder_1 (.a(shifter_1_out), .b(in_2), .out(_01));  // open: cin, cout
  Subtractor subtractor_1 (.a(shifter_2_out), .b(in_2), .out(_10));  // open: bin, bout
  assign _11 = shifter_3_out ^ in_2;  // XOR_Gate xor_1, 8 bits wide

  // Other names for the same wires on the sheet: clk = in_3; op[1:0] = in_1; operand[7:0] = in_2
endmodule
