// Logisim project intelligent_elevator.circ as structural Verilog: 9 circuits, main circuit main
module main (
  input  [7:0] in_1,
  input  [7:0] in_2,
  input  [7:0] in_3,
  input  [7:0] in_4,
  input  [3:0] in_5,
  output [7:0] out_6
);

  wire comparator_1_eq, comparator_2_eq, comparator_3_eq, comparator_4_lt, comparator_5_lt, comparator_6_lt,
       comparator_7_lt;
  wire [1:0] big1, big2, big3, big4, from, multiplexer_1_out, multiplexer_2_out, multiplexer_3_out,
       multiplexer_4_out, multiplexer_5_out, multiplexer_6_out, multiplexer_7_out, negator_1_out,
       negator_2_out, negator_3_out, negator_4_out, subtractor_1_out, subtractor_2_out, subtractor_3_out,
       subtractor_4_out;
  wire [7:0] adder_1_out, adder_2_out, bit_extender_1_out, bit_extender_2_out, bit_extender_3_out,
       bit_extender_4_out;
  wire [9:2] n10bit_sort_1_out_5, n10bit_sort_1_out_6, n10bit_sort_1_out_7, n10bit_sort_1_out_8;

  BitFinder #(.width(4), .\type ("high1")) bitfinder_1 (.in(in_5), .index(from));  // open: found
  _10bit_sort u_10bit_sort_1 (
    .in_1({in_1, 2'b00}), .in_2({in_2, 2'b01}), .in_3({in_3, 2'b10}), .in_4({in_4, 2'b11}),
    .out_5({n10bit_sort_1_out_5, big4}), .out_6({n10bit_sort_1_out_6, big3}),
    .out_7({n10bit_sort_1_out_7, big2}), .out_8({n10bit_sort_1_out_8, big1}));
  // Probe on from
  Comparator #(.width(2), .mode("unsigned")) comparator_1 (.a(big2), .b(from), .eq(comparator_1_eq));  // open: gt, lt
  Comparator #(.width(2), .mode("unsigned")) comparator_2 (.a(big3), .b(from), .eq(comparator_2_eq));  // open: gt, lt
  Comparator #(.width(2), .mode("unsigned")) comparator_3 (.a(big4), .b(from), .eq(comparator_3_eq));  // open: gt, lt
  Multiplexer #(.width(2), .enable("false")) multiplexer_1 (
    .in0(big2), .in1(big1), .out(multiplexer_1_out), .sel(comparator_1_eq));
  // Probe on multiplexer_1_out
  Multiplexer #(.width(2), .enable("false")) multiplexer_2 (
    .in0(big3), .in1(multiplexer_1_out), .out(multiplexer_2_out), .sel(comparator_2_eq));
  Multiplexer #(.width(2), .enable("false")) multiplexer_3 (
    .in0(big4), .in1(multiplexer_2_out), .out(multiplexer_3_out), .sel(comparator_3_eq));
  Subtractor #(.width(2)) subtractor_1 (.a(big1), .b(from), .out(subtractor_1_out));  // open: bin, bout
  Comparator #(.width(2), .mode("unsigned")) comparator_4 (.a(big1), .b(from), .lt(comparator_4_lt));  // open: gt, eq
  Subtractor #(.width(2)) subtractor_2 (.a(big1), .b(multiplexer_1_out), .out(subtractor_2_out));  // open: bin, bout
  Comparator #(.width(2), .mode("unsigned")) comparator_5 (
    .a(big1), .b(multiplexer_1_out), .lt(comparator_5_lt));  // open: gt, eq
  Subtractor #(.width(2)) subtractor_3 (
    .a(multiplexer_1_out), .b(multiplexer_2_out), .out(subtractor_3_out));  // open: bin, bout
  Comparator #(.width(2), .mode("unsigned")) comparator_6 (
    .a(multiplexer_1_out), .b(multiplexer_2_out), .lt(comparator_6_lt));  // open: gt, eq
  Subtractor #(.width(2)) subtractor_4 (
    .a(multiplexer_2_out), .b(multiplexer_3_out), .out(subtractor_4_out));  // open: bin, bout
  Comparator #(.width(2), .mode("unsigned")) comparator_7 (
    .a(multiplexer_2_out), .b(multiplexer_3_out), .lt(comparator_7_lt));  // open: gt, eq
  Multiplexer #(.width(2), .enable("false")) multiplexer_4 (
    .in0(subtractor_1_out), .in1(negator_1_out), .out(multiplexer_4_out), .sel(comparator_4_lt));
  Negator #(.width(2)) negator_1 (.in(subtractor_1_out), .out(negator_1_out));
  Multiplexer #(.width(2), .enable("false")) multiplexer_5 (
    .in0(subtractor_2_out), .in1(negator_2_out), .out(multiplexer_5_out), .sel(comparator_5_lt));
  Negator #(.width(2)) negator_2 (.in(subtractor_2_out), .out(negator_2_out));
  Multiplexer #(.width(2), .enable("false")) multiplexer_6 (
    .in0(subtractor_3_out), .in1(negator_3_out), .out(multiplexer_6_out), .sel(comparator_6_lt));
  Negator #(.width(2)) negator_3 (.in(subtractor_3_out), .out(negator_3_out));
  Multiplexer #(.width(2), .enable("false")) multiplexer_7 (
    .in0(subtractor_4_out), .in1(negator_4_out), .out(multiplexer_7_out), .sel(comparator_7_lt));
  Negator #(.width(2)) negator_4 (.in(subtractor_4_out), .out(negator_4_out));
  assign bit_extender_1_out = {{6{1'b0}}, multiplexer_4_out};  // Bit_Extender bit_extender_1
  assign bit_extender_2_out = {{6{1'b0}}, multiplexer_5_out};  // Bit_Extender bit_extender_2
  // Probe on bit_extender_3_out
  assign bit_extender_3_out = {{6{1'b0}}, multiplexer_6_out};  // Bit_Extender bit_extender_3
  // Probe on bit_extender_4_out
  assign bit_extender_4_out = {{6{1'b0}}, multiplexer_7_out};  // Bit_Extender bit_extender_4
  // Probe on bit_extender_1_out
  Adder adder_1 (.a(bit_extender_1_out), .b(bit_extender_2_out), .out(adder_1_out));  // open: cin, cout
  // Probe on bit_extender_2_out
  Adder adder_2 (.a(bit_extender_3_out), .b(bit_extender_4_out), .out(adder_2_out));  // open: cin, cout
  Adder adder_3 (.a(adder_1_out), .b(adder_2_out), .out(out_6));  // open: cin, cout
  // AND_Gate and_1 is placed but not wired

  // Other names for the same wires on the sheet: num0[9:2] = in_1; num1[9:2] = in_2; num2[9:2] = in_3;
  //   num3[9:2] = in_4
endmodule

module _1bit_swap (
  input  in_1,
  input  in_2,
  input  in_3,
  output out_4,
  output out_5
);

  wire and_1_out, and_2_out, and_3_out, and_4_out, not_1_out;

  not not_1 (not_1_out, in_3);
  and and_1 (and_1_out, in_1, not_1_out);
  and and_2 (and_2_out, in_2, in_3);
  and and_3 (and_3_out, in_2, not_1_out);
  and and_4 (and_4_out, in_1, in_3);
  or or_1 (out_4, and_1_out, and_2_out);
  or or_2 (out_5, and_3_out, and_4_out);
endmodule

module _4bit_swap (
  input  [3:0] in_1,
  input  [3:0] in_2,
  input  in_3,
  output [3:0] out_4,
  output [3:0] out_5
);

  _1bit_swap u_1bit_swap_1 (.in_1(in_1[0]), .in_2(in_2[0]), .in_3(in_3), .out_4(out_4[0]), .out_5(out_5[0]));
  _1bit_swap u_1bit_swap_2 (.in_1(in_1[1]), .in_2(in_2[1]), .in_3(in_3), .out_4(out_4[1]), .out_5(out_5[1]));
  _1bit_swap u_1bit_swap_3 (.in_1(in_1[2]), .in_2(in_2[2]), .in_3(in_3), .out_4(out_4[2]), .out_5(out_5[2]));
  _1bit_swap u_1bit_swap_4 (.in_1(in_1[3]), .in_2(in_2[3]), .in_3(in_3), .out_4(out_4[3]), .out_5(out_5[3]));
endmodule

module _4bit_sort (
  input  [3:0] in_1,
  input  [3:0] in_2,
  input  [3:0] in_3,
  input  [3:0] in_4,
  output [3:0] out_5,
  output [3:0] out_6,
  output [3:0] out_7,
  output [3:0] out_8
);

  wire [3:0] n4bit_compare_swap_1_out_4, n4bit_compare_swap_1_smaller, n4bit_compare_swap_2_out_4,
       n4bit_compare_swap_2_smaller, n4bit_compare_swap_3_out_4, n4bit_compare_swap_3_smaller,
       n4bit_compare_swap_4_out_4, n4bit_compare_swap_6_out_4;

  _4bit_compare_swap u_4bit_compare_swap_1 (
    .in_1(in_1), .in_2(in_2), .smaller(n4bit_compare_swap_1_smaller), .out_4(n4bit_compare_swap_1_out_4));
  _4bit_compare_swap u_4bit_compare_swap_2 (
    .in_1(n4bit_compare_swap_1_smaller), .in_2(in_3), .smaller(n4bit_compare_swap_2_smaller),
    .out_4(n4bit_compare_swap_2_out_4));
  _4bit_compare_swap u_4bit_compare_swap_3 (
    .in_1(n4bit_compare_swap_2_out_4), .in_2(n4bit_compare_swap_1_out_4),
    .smaller(n4bit_compare_swap_3_smaller), .out_4(n4bit_compare_swap_3_out_4));
  _4bit_compare_swap u_4bit_compare_swap_4 (
    .in_1(n4bit_compare_swap_2_smaller), .in_2(in_4), .smaller(out_5), .out_4(n4bit_compare_swap_4_out_4));
  _4bit_compare_swap u_4bit_compare_swap_5 (
    .in_1(n4bit_compare_swap_6_out_4), .in_2(n4bit_compare_swap_3_out_4), .smaller(out_7), .out_4(out_8));
  _4bit_compare_swap u_4bit_compare_swap_6 (
    .in_1(n4bit_compare_swap_4_out_4), .in_2(n4bit_compare_swap_3_smaller), .smaller(out_6),
    .out_4(n4bit_compare_swap_6_out_4));
endmodule

module _4bit_compare_swap (
  input  [3:0] in_1,
  input  [3:0] in_2,
  output [3:0] smaller,
  output [3:0] out_4
);

  wire comparator_1_gt;

  Comparator #(.width(4), .mode("unsigned")) comparator_1 (.a(in_1), .b(in_2), .gt(comparator_1_gt));  // open: eq, lt
  _4bit_swap u_4bit_swap_1 (.in_1(in_1), .in_2(in_2), .in_3(comparator_1_gt), .out_4(smaller), .out_5(out_4));
endmodule

module _8bit_swap (
  input  [7:0] in_1,
  input  [7:0] in_2,
  input  in_3,
  output [7:0] out_4,
  output [7:0] out_5
);

  _1bit_swap u_1bit_swap_1 (.in_1(in_1[0]), .in_2(in_2[0]), .in_3(in_3), .out_4(out_4[0]), .out_5(out_5[0]));
  _1bit_swap u_1bit_swap_2 (.in_1(in_1[1]), .in_2(in_2[1]), .in_3(in_3), .out_4(out_4[1]), .out_5(out_5[1]));
  _1bit_swap u_1bit_swap_3 (.in_1(in_1[2]), .in_2(in_2[2]), .in_3(in_3), .out_4(out_4[2]), .out_5(out_5[2]));
  _1bit_swap u_1bit_swap_4 (.in_1(in_1[3]), .in_2(in_2[3]), .in_3(in_3), .out_4(out_4[3]), .out_5(out_5[3]));
  _1bit_swap u_1bit_swap_5 (.in_1(in_1[4]), .in_2(in_2[4]), .in_3(in_3), .out_4(out_4[4]), .out_5(out_5[4]));
  _1bit_swap u_1bit_swap_6 (.in_1(in_1[5]), .in_2(in_2[5]), .in_3(in_3), .out_4(out_4[5]), .out_5(out_5[5]));
  _1bit_swap u_1bit_swap_7 (.in_1(in_1[6]), .in_2(in_2[6]), .in_3(in_3), .out_4(out_4[6]), .out_5(out_5[6]));
  _1bit_swap u_1bit_swap_8 (.in_1(in_1[7]), .in_2(in_2[7]), .in_3(in_3), .out_4(out_4[7]), .out_5(out_5[7]));
endmodule

module _10bit_swap (
  input  [9:0] in_1,
  input  [9:0] in_2,
  input  in_3,
  output [9:0] out_4,
  output [9:0] out_5
);

  _1bit_swap u_1bit_swap_1 (.in_1(in_1[0]), .in_2(in_2[0]), .in_3(in_3), .out_4(out_4[0]), .out_5(out_5[0]));
  _1bit_swap u_1bit_swap_2 (.in_1(in_1[1]), .in_2(in_2[1]), .in_3(in_3), .out_4(out_4[1]), .out_5(out_5[1]));
  _1bit_swap u_1bit_swap_3 (.in_1(in_1[2]), .in_2(in_2[2]), .in_3(in_3), .out_4(out_4[2]), .out_5(out_5[2]));
  _1bit_swap u_1bit_swap_4 (.in_1(in_1[3]), .in_2(in_2[3]), .in_3(in_3), .out_4(out_4[3]), .out_5(out_5[3]));
  _1bit_swap u_1bit_swap_5 (.in_1(in_1[4]), .in_2(in_2[4]), .in_3(in_3), .out_4(out_4[4]), .out_5(out_5[4]));
  _1bit_swap u_1bit_swap_6 (.in_1(in_1[5]), .in_2(in_2[5]), .in_3(in_3), .out_4(out_4[5]), .out_5(out_5[5]));
  _1bit_swap u_1bit_swap_7 (.in_1(in_1[6]), .in_2(in_2[6]), .in_3(in_3), .out_4(out_4[6]), .out_5(out_5[6]));
  _1bit_swap u_1bit_swap_8 (.in_1(in_1[7]), .in_2(in_2[7]), .in_3(in_3), .out_4(out_4[7]), .out_5(out_5[7]));
  _1bit_swap u_1bit_swap_9 (.in_1(in_1[8]), .in_2(in_2[8]), .in_3(in_3), .out_4(out_4[8]), .out_5(out_5[8]));
  _1bit_swap u_1bit_swap_10 (.in_1(in_1[9]), .in_2(in_2[9]), .in_3(in_3), .out_4(out_4[9]), .out_5(out_5[9]));
endmodule

module _10bit_compare_swap (
  input  [9:0] in_1,
  input  [9:0] in_2,
  output [9:0] smaller,
  output [9:0] out_4
);

  wire comparator_1_gt;

  Comparator #(.width(10), .mode("unsigned")) comparator_1 (.a(in_1), .b(in_2), .gt(comparator_1_gt));  // open: eq, lt
  _10bit_swap u_10bit_swap_1 (.in_1(in_1), .in_2(in_2), .in_3(comparator_1_gt), .out_4(smaller), .out_5(out_4));
endmodule

module _10bit_sort (
  input  [9:0] in_1,
  input  [9:0] in_2,
  input  [9:0] in_3,
  input  [9:0] in_4,
  output [9:0] out_5,
  output [9:0] out_6,
  output [9:0] out_7,
  output [9:0] out_8
);

  wire [9:0] n10bit_compare_swap_1_out_4, n10bit_compare_swap_1_smaller, n10bit_compare_swap_2_out_4,
       n10bit_compare_swap_2_smaller, n10bit_compare_swap_3_out_4, n10bit_compare_swap_3_smaller,
       n10bit_compare_swap_4_out_4, n10bit_compare_swap_5_out_4;

  _10bit_compare_swap u_10bit_compare_swap_1 (
    .in_1(in_1), .in_2(in_2), .smaller(n10bit_compare_swap_1_smaller), .out_4(n10bit_compare_swap_1_out_4));
  _10bit_compare_swap u_10bit_compare_swap_2 (
    .in_1(n10bit_compare_swap_1_smaller), .in_2(in_3), .smaller(n10bit_compare_swap_2_smaller),
    .out_4(n10bit_compare_swap_2_out_4));
  _10bit_compare_swap u_10bit_compare_swap_3 (
    .in_1(n10bit_compare_swap_2_out_4), .in_2(n10bit_compare_swap_1_out_4),
    .smaller(n10bit_compare_swap_3_smaller), .out_4(n10bit_compare_swap_3_out_4));
  _10bit_compare_swap u_10bit_compare_swap_4 (
    .in_1(n10bit_compare_swap_2_smaller), .in_2(in_4), .smaller(out_5), .out_4(n10bit_compare_swap_4_out_4));
  _10bit_compare_swap u_10bit_compare_swap_5 (
    .in_1(n10bit_compare_swap_4_out_4), .in_2(n10bit_compare_swap_3_smaller), .smaller(out_6),
    .out_4(n10bit_compare_swap_5_out_4));
  _10bit_compare_swap u_10bit_compare_swap_6 (
    .in_1(n10bit_compare_swap_5_out_4), .in_2(n10bit_compare_swap_3_out_4), .smaller(out_7), .out_4(out_8));
endmodule
