// Logisim project intelligent_elevator_zhp.circ as structural Verilog: 4 circuits, main circuit main
module main (
  input  [3:0] from,
  input  [7:0] num0,
  input  [7:0] num1,
  input  [7:0] num2,
  input  [7:0] num3,
  output [7:0] \output 
);

  wire comparator_1_eq, comparator_2_eq, comparator_3_eq, comparator_4_eq;
  wire [1:0] abs_1_cha, abs_2_cha, abs_3_cha, first, last, m1, second, third;
  wire [7:0] adder_1_out, bit_extender_1_out, bit_extender_2_out, bit_extender_3_out;
  wire [9:0] A, B, C, D;
  wire [9:2] sort4_1__0, sort4_1__1, sort4_1__2, sort4_1__3;

  Priority_Encoder #(.select(2)) priority_encoder_1 (
    .in0(from[0]), .in1(from[1]), .in2(from[2]), .in3(from[3]), .out(m1));  // open: gs, en_out, en_in
  Comparator #(.width(2), .mode("unsigned")) comparator_1 (.a(2'b00), .b(m1), .eq(comparator_1_eq));  // open: gt, lt
  Multiplexer #(.width(10), .enable("false")) multiplexer_1 (
    .in0({num0, 2'b00}), .in1({10{1'b0}}), .out(A), .sel(comparator_1_eq));
  Multiplexer #(.width(10), .enable("false")) multiplexer_2 (
    .in0({num1, 2'b01}), .in1(10'h1), .out(B), .sel(comparator_2_eq));
  Comparator #(.width(2), .mode("unsigned")) comparator_2 (.a(2'b01), .b(m1), .eq(comparator_2_eq));  // open: gt, lt
  Multiplexer #(.width(10), .enable("false")) multiplexer_3 (
    .in0({num2, 2'b10}), .in1(10'h2), .out(C), .sel(comparator_3_eq));
  Comparator #(.width(2), .mode("unsigned")) comparator_3 (.a(2'b10), .b(m1), .eq(comparator_3_eq));  // open: gt, lt
  Multiplexer #(.width(10), .enable("false")) multiplexer_4 (
    .in0({num3, 2'b11}), .in1(10'h3), .out(D), .sel(comparator_4_eq));
  Comparator #(.width(2), .mode("unsigned")) comparator_4 (.a(2'b11), .b(m1), .eq(comparator_4_eq));  // open: gt, lt
  sort4 sort4_1 (
    .a(A), .b(B), .c(C), .d(D), ._0({sort4_1__0, first}), ._1({sort4_1__1, second}),
    ._2({sort4_1__2, third}), ._3({sort4_1__3, last}));
  abs abs_1 (.a(m1), .b(first), .cha(abs_1_cha));
  abs abs_2 (.a(second), .b(first), .cha(abs_2_cha));
  assign bit_extender_1_out = {{6{1'b0}}, abs_1_cha};  // Bit_Extender bit_extender_1
  assign bit_extender_2_out = {{6{1'b0}}, abs_2_cha};  // Bit_Extender bit_extender_2
  abs abs_3 (.a(second), .b(third), .cha(abs_3_cha));
  assign bit_extender_3_out = {{6{1'b0}}, abs_3_cha};  // Bit_Extender bit_extender_3
  Adder adder_1 (.a(bit_extender_1_out), .b(bit_extender_2_out), .out(adder_1_out));  // open: cin, cout
  Adder adder_2 (.a(adder_1_out), .b(bit_extender_3_out), .out(\output ));  // open: cin, cout
endmodule

module max2 (
  input  [9:0] A,
  input  [9:0] B,
  output [9:0] max,
  output [9:0] min
);

  wire fl;

  Comparator #(.width(10), .mode("unsigned")) comparator_1 (.a(A), .b(B), .lt(fl));  // open: gt, eq
  Multiplexer #(.width(10), .enable("false")) multiplexer_1 (.in0(A), .in1(B), .out(max), .sel(fl));
  assign min = max ^ A ^ B;  // XOR_Gate xor_1, 10 bits wide
endmodule

module sort4 (
  input  [9:0] a,
  input  [9:0] b,
  input  [9:0] c,
  input  [9:0] d,
  output [9:0] _0,
  output [9:0] _1,
  output [9:0] _2,
  output [9:0] _3
);

  wire [9:0] b1, c1, d1, max2_1_max, max2_2_max, max2_2_min, max2_3_max, max2_4_min;

  max2 max2_1 (.A(a), .B(b), .max(max2_1_max), .min(b1));
  max2 max2_2 (.A(b1), .B(c1), .max(max2_2_max), .min(max2_2_min));
  max2 max2_3 (.A(max2_1_max), .B(c), .max(max2_3_max), .min(c1));
  max2 max2_4 (.A(max2_2_max), .B(d1), .max(_1), .min(max2_4_min));
  max2 max2_5 (.A(max2_2_min), .B(max2_4_min), .max(_2), .min(_3));
  max2 max2_6 (.A(max2_3_max), .B(d), .max(_0), .min(d1));
endmodule

module abs (
  input  [1:0] a,
  input  [1:0] b,
  output [1:0] cha
);

  wire fl;
  wire [1:0] subtractor_1_out, subtractor_2_out;

  Comparator #(.width(2), .mode("unsigned")) comparator_1 (.a(a), .b(b), .lt(fl));  // open: gt, eq
  Subtractor #(.width(2)) subtractor_1 (.a(a), .b(b), .out(subtractor_1_out));  // open: bin, bout
  Subtractor #(.width(2)) subtractor_2 (.a(b), .b(a), .out(subtractor_2_out));  // open: bin, bout
  Multiplexer #(.width(2), .enable("false")) multiplexer_1 (
    .in0(subtractor_1_out), .in1(subtractor_2_out), .out(cha), .sel(fl));
endmodule
