// Logisim project ups_and_downs.circ as structural Verilog: 1 circuit, main circuit main
module main (
  input  [4:0] in_1,
  input  in_2,
  input  in_3,
  output out_4
);

  wire up;
  wire [2:0] _000, _001, _010, _011, _100, multiplexer_3_out, status;
  wire [4:0] register_2_q, xor_1_out, xor_2_out;

  assign xor_1_out = 5'b00111 ^ in_1;  // XOR_Gate xor_1, 5 bits wide
  Multiplexer #(.width(3), .enable("false")) multiplexer_1 (.in0(3'b000), .in1(3'b001), .out(_000), .sel(up));
  Multiplexer #(.width(3), .enable("false")) multiplexer_2 (.in0(3'b000), .in1(3'b100), .out(_011), .sel(up));
  // Probe on _011
  // Probe on multiplexer_3_out
  // Probe on status
  Register #(.width(3)) register_1 (.D(multiplexer_3_out), .Q(status), .clk(in_2), .clr(in_3));  // open: en
  Multiplexer #(.select(3), .width(3), .enable("false")) multiplexer_3 (
    .in0(_000), .in1(_001), .in2(_010), .in3(_011), .in4(_100), .out(multiplexer_3_out), .sel(status));  // open: in5, in6, in7
  Comparator #(.width(3), .mode("unsigned")) comparator_1 (.a(status), .b(3'b100), .eq(out_4));  // open: gt, lt
  Register #(.width(5)) register_2 (.D(xor_1_out), .Q(register_2_q), .clk(in_2), .clr(in_3));  // open: en
  Multiplexer #(.width(3), .enable("false")) multiplexer_4 (.in0(3'b000), .in1(3'b010), .out(_001), .sel(up));
  Multiplexer #(.width(3), .enable("false")) multiplexer_5 (.in0(3'b000), .in1(3'b010), .out(_100), .sel(up));
  Comparator #(.width(5), .mode("unsigned")) comparator_2 (.a(in_1), .b(xor_2_out), .gt(up));  // open: eq, lt
  assign xor_2_out = 5'b00111 ^ register_2_q;  // XOR_Gate xor_2, 5 bits wide
  // Probe on xor_2_out
  Multiplexer #(.width(3), .enable("false")) multiplexer_6 (.in0(3'b011), .in1(3'b010), .out(_010), .sel(up));

  // Other names for the same wires on the sheet: a[4:0] = in_1; clk = in_2; output = out_4; reset = in_3
endmodule
