// Logisim project cpu2.circ as structural Verilog: 10 circuits, main circuit main
module main (
  input  in_1,
  output [31:0] out_2,
  output [31:0] out_3,
  output out_4,
  output [4:0] out_5,
  output [31:0] out_6,
  output out_7,
  output [31:0] out_8,
  output [31:0] out_9
);

  wire Addr2Reg, ALUSrc, and_1_out, clk, comparator_1_eq, comparator_2_eq, equal, EXTOp, Mem2Reg,
       multiplexer_5_out, RegDst, zero;
  wire [1:0] NPC_Sel;
  wire [3:0] \type ;
  wire [4:0] multiplexer_2_out;
  wire [10:0] imm;
  wire [15:0] imm16;
  wire [25:0] imm26;
  wire [31:0] adder_1_out, adder_2_out, Data, imm32, multiplexer_3_out, multiplexer_4_out, multiplexer_7_out,
       NPC, RD1;

  Clock clock_1 (.out(clk));
  NPC npc_1 (
    .in_1(out_3), .in_2(imm16), .in_6(NPC_Sel), .in_7(zero), .out_8(NPC), .in_3(imm26), .in_5(equal),
    .in_4(imm));
  PC pc_1 (.in_1(NPC), .out_4(out_3), .in_3(in_1), .in_2(clk));
  IM im_1 (.in_1(out_3), .out_2(out_2));
  Adder #(.width(32)) adder_1 (.a(out_3), .b(32'h4), .out(adder_1_out));  // open: cin, cout
  Controller controller_1 (
    .in_1(out_2[31:26]), .out_3(NPC_Sel), .in_2(out_2[5:0]), .out_7(out_4), .out_4(\type ), .out_8(EXTOp),
    .out_9(ALUSrc), .out_5(RegDst), .out_10(out_7), .out_6(Mem2Reg), .out_11(Addr2Reg));
  Bit_Extender #(.in_width(32)) bit_extender_1 (.in(out_2), .out(imm16));
  Bit_Extender #(.in_width(32), .out_width(26)) bit_extender_2 (.in(out_2), .out(imm26));
  Bit_Extender #(.in_width(32), .out_width(11)) bit_extender_3 (.in(out_2), .out(imm));
  Adder #(.width(32)) adder_2 (.a(32'h3000), .b(adder_1_out), .out(adder_2_out));  // open: cin, cout
  Multiplexer #(.width(5), .enable("false")) multiplexer_1 (
    .in0(out_2[20:16]), .in1(multiplexer_2_out), .out(out_5), .sel(RegDst));
  Multiplexer #(.width(5), .enable("false")) multiplexer_2 (
    .in0(out_2[15:11]), .in1({5{1'b1}}), .out(multiplexer_2_out), .sel(Addr2Reg));
  Comparator #(.width(4), .mode("unsigned")) comparator_1 (
    .a(\type ), .b(4'b1100), .eq(comparator_1_eq));  // open: gt, lt
  Multiplexer #(.width(32), .enable("false")) multiplexer_3 (
    .in0(out_8), .in1(adder_2_out), .out(multiplexer_3_out), .sel(comparator_1_eq));
  EXT ext_1 (.in_1(imm16), .in_2(EXTOp), .out_3(imm32));
  Multiplexer #(.width(32), .enable("false")) multiplexer_4 (
    .in0(multiplexer_3_out), .in1(adder_1_out), .out(multiplexer_4_out), .sel(Addr2Reg));
  Comparator #(.width(4), .mode("unsigned")) comparator_2 (
    .a(\type ), .b(4'b1100), .eq(comparator_2_eq));  // open: gt, lt
  Multiplexer #(.enable("false")) multiplexer_5 (
    .in0(1'b1), .in1(equal), .out(multiplexer_5_out), .sel(comparator_2_eq));
  and and_1 (and_1_out, multiplexer_5_out, out_4);
  // Probe on out_6
  Multiplexer #(.width(32), .enable("false")) multiplexer_6 (
    .in0(multiplexer_4_out), .in1(Data), .out(out_6), .sel(Mem2Reg));
  GRF grf_1 (
    .in_1(out_6), .in_2(clk), .in_3(in_1), .in_4(and_1_out), .in_5(out_2[25:21]), .in_6(out_2[20:16]),
    .in_7(out_5), .out_8(RD1), .out_9(out_9));
  // Probe on out_2[25:21]
  Multiplexer #(.width(32), .enable("false")) multiplexer_7 (
    .in0(out_9), .in1(imm32), .out(multiplexer_7_out), .sel(ALUSrc));
  DM dm_1 (.in_1(out_8), .in_2(out_9), .in_3(out_7), .in_4(clk), .in_5(in_1), .out_6(Data));
  ALU alu_1 (.in_1(RD1), .in_2(multiplexer_7_out), .in_3(\type ), .out_4(out_8), .out_5(zero), .out_6(equal));

  // Other names for the same wires on the sheet: Funct[5:0] = out_2[5:0]; Insn[31:0] = out_2; rd[4:0] = out_2[15:11];
  //   rt[4:0] = out_2[20:16]; rs[4:0] = out_2[25:21]; OpCode[5:0] = out_2[31:26]; MemWr = out_7; PC[31:0] = out_3;
  //   RD2[31:0] = out_9; RegAddr[4:0] = out_5; reset = in_1; result[31:0] = out_8; RFWr = out_4; WD[31:0] = out_6
endmodule

module IM (
  input  [31:0] in_1,
  output [31:0] out_2
);

  wire [31:0] subtractor_1_out;

  Subtractor #(.width(32)) subtractor_1 (.a(in_1), .b(32'h3000), .out(subtractor_1_out));  // open: bin, bout
  ROM #(.addrWidth(12), .dataWidth(32)) rom_1 (.addr(subtractor_1_out[13:2]), .data(out_2));  // open: sel

  // Notes on the sheet:
  //   contents of rom_1 (hex, n*v repeats v):
  //   34080009 34090008 65285010
endmodule

module PC (
  input  [31:0] in_1,
  input  in_2,
  input  in_3,
  output [31:0] out_4
);

  wire [31:0] register_1_q, xor_1_out;

  assign xor_1_out = 32'h3000 ^ in_1;  // XOR_Gate xor_1, 32 bits wide
  Register #(.width(32)) register_1 (.D(xor_1_out), .Q(register_1_q), .clk(in_2), .clr(in_3));  // open: en
  assign out_4 = 32'h3000 ^ register_1_q;  // XOR_Gate xor_2, 32 bits wide
endmodule

module NPC (
  input  [31:0] in_1,
  input  [15:0] in_2,
  input  [25:0] in_3,
  input  [10:0] in_4,
  input  in_5,
  input  [1:0] in_6,
  input  in_7,
  output [31:0] out_8
);

  wire [31:0] adder_2_out, adder_3_out, bit_extender_1_out, bit_extender_2_out, multiplexer_1_out,
       multiplexer_2_out, PC___4, shifter_1_out, shifter_2_out;

  assign bit_extender_1_out = {{16{in_2[15]}}, in_2};  // Bit_Extender bit_extender_1
  assign bit_extender_2_out = {{21{in_4[10]}}, in_4};  // Bit_Extender bit_extender_2
  Adder #(.width(32)) adder_1 (.a(in_1), .b(32'h4), .out(PC___4));  // open: cin, cout
  Shifter #(.width(32)) shifter_1 (.in(bit_extender_1_out), .\dist (5'b00010), .out(shifter_1_out));
  Shifter #(.width(32)) shifter_2 (.in(bit_extender_2_out), .\dist (5'b00010), .out(shifter_2_out));
  Adder #(.width(32)) adder_2 (.a(PC___4), .b(shifter_1_out), .out(adder_2_out));  // open: cin, cout
  Adder #(.width(32)) adder_3 (.a(PC___4), .b(shifter_2_out), .out(adder_3_out));  // open: cin, cout
  Multiplexer #(.width(32), .enable("false")) multiplexer_1 (
    .in0(PC___4), .in1(adder_2_out), .out(multiplexer_1_out), .sel(in_7));
  Multiplexer #(.width(32), .enable("false")) multiplexer_2 (
    .in0(PC___4), .in1(adder_3_out), .out(multiplexer_2_out), .sel(in_5));
  Multiplexer #(.select(2), .width(32), .enable("false")) multiplexer_3 (
    .in0(PC___4), .in1(multiplexer_1_out), .in2({PC___4[31:28], in_3, 2'b00}), .in3(multiplexer_2_out),
    .out(out_8), .sel(in_6));

  // Other names for the same wires on the sheet: equal = in_5; NPC_Sel[1:0] = in_6; zero = in_7
endmodule

module GRF (
  input  [31:0] in_1,
  input  in_2,
  input  in_3,
  input  in_4,
  input  [4:0] in_5,
  input  [4:0] in_6,
  input  [4:0] in_7,
  output [31:0] out_8,
  output [31:0] out_9
);

  wire [31:0] R0_out, R1_in, R1_out, R2_in, R2_out, R3_in, R3_out, R4_in, R4_out, R5_in, R5_out, R6_in,
       R6_out, R7_in, R7_out, R8_in, R8_out, R9_in, R9_out, R10_in, R10_out, R11_in, R11_out, R12_in,
       R12_out, R13_in, R13_out, R14_in, R14_out, R15_in, R15_out, R16_in, R16_out, R17_in, R17_out, R18_in,
       R18_out, R19_in, R19_out, R20_in, R20_out, R21_in, R21_out, R22_in, R22_out, R23_in, R23_out, R24_in,
       R24_out, R25_in, R25_out, R26_in, R26_out, R27_in, R27_out, R28_in, R28_out, R29_in, R29_out, R30_in,
       R30_out, R31_in, R31_out;

  Register #(.width(32)) register_1 (.en(in_4), .Q(R0_out), .clk(in_2), .clr(in_3));  // open: D
  Register #(.width(32)) register_2 (.D(R8_in), .en(in_4), .Q(R8_out), .clk(in_2), .clr(in_3));
  Register #(.width(32)) register_3 (.D(R16_in), .en(in_4), .Q(R16_out), .clk(in_2), .clr(in_3));
  Register #(.width(32)) register_4 (.D(R24_in), .en(in_4), .Q(R24_out), .clk(in_2), .clr(in_3));
  Multiplexer #(.select(5), .width(32), .enable("false")) multiplexer_1 (
    .in0(R0_out), .in1(R1_out), .in2(R2_out), .in3(R3_out), .in4(R4_out), .in5(R5_out), .in6(R6_out),
    .in7(R7_out), .in8(R8_out), .in9(R9_out), .in10(R10_out), .in11(R11_out), .in12(R12_out), .in13(R13_out),
    .in14(R14_out), .in15(R15_out), .in16(R16_out), .in17(R17_out), .in18(R18_out), .in19(R19_out),
    .in20(R20_out), .in21(R21_out), .in22(R22_out), .in23(R23_out), .in24(R24_out), .in25(R25_out),
    .in26(R26_out), .in27(R27_out), .in28(R28_out), .in29(R29_out), .in30(R30_out), .in31(R31_out),
    .out(out_8), .sel(in_5));
  Register #(.width(32)) register_5 (.D(R1_in), .en(in_4), .Q(R1_out), .clk(in_2), .clr(in_3));
  Register #(.width(32)) register_6 (.D(R9_in), .en(in_4), .Q(R9_out), .clk(in_2), .clr(in_3));
  Register #(.width(32)) register_7 (.D(R17_in), .en(in_4), .Q(R17_out), .clk(in_2), .clr(in_3));
  Register #(.width(32)) register_8 (.D(R25_in), .en(in_4), .Q(R25_out), .clk(in_2), .clr(in_3));
  Register #(.width(32)) register_9 (.D(R2_in), .en(in_4), .Q(R2_out), .clk(in_2), .clr(in_3));
  Register #(.width(32)) register_10 (.D(R10_in), .en(in_4), .Q(R10_out), .clk(in_2), .clr(in_3));
  Register #(.width(32)) register_11 (.D(R18_in), .en(in_4), .Q(R18_out), .clk(in_2), .clr(in_3));
  Register #(.width(32)) register_12 (.D(R26_in), .en(in_4), .Q(R26_out), .clk(in_2), .clr(in_3));
  Multiplexer #(.select(5), .width(32), .enable("false")) multiplexer_2 (
    .in0(R0_out), .in1(R1_out), .in2(R2_out), .in3(R3_out), .in4(R4_out), .in5(R5_out), .in6(R6_out),
    .in7(R7_out), .in8(R8_out), .in9(R9_out), .in10(R10_out), .in11(R11_out), .in12(R12_out), .in13(R13_out),
    .in14(R14_out), .in15(R15_out), .in16(R16_out), .in17(R17_out), .in18(R18_out), .in19(R19_out),
    .in20(R20_out), .in21(R21_out), .in22(R22_out), .in23(R23_out), .in24(R24_out), .in25(R25_out),
    .in26(R26_out), .in27(R27_out), .in28(R28_out), .in29(R29_out), .in30(R30_out), .in31(R31_out),
    .out(out_9), .sel(in_6));
  Register #(.width(32)) register_13 (.D(R3_in), .en(in_4), .Q(R3_out), .clk(in_2), .clr(in_3));
  Register #(.width(32)) register_14 (.D(R11_in), .en(in_4), .Q(R11_out), .clk(in_2), .clr(in_3));
  Register #(.width(32)) register_15 (.D(R19_in), .en(in_4), .Q(R19_out), .clk(in_2), .clr(in_3));
  Register #(.width(32)) register_16 (.D(R27_in), .en(in_4), .Q(R27_out), .clk(in_2), .clr(in_3));
  Register #(.width(32)) register_17 (.D(R4_in), .en(in_4), .Q(R4_out), .clk(in_2), .clr(in_3));
  Register #(.width(32)) register_18 (.D(R12_in), .en(in_4), .Q(R12_out), .clk(in_2), .clr(in_3));
  Register #(.width(32)) register_19 (.D(R20_in), .en(in_4), .Q(R20_out), .clk(in_2), .clr(in_3));
  Register #(.width(32)) register_20 (.D(R28_in), .en(in_4), .Q(R28_out), .clk(in_2), .clr(in_3));
  Demultiplexer #(.select(5), .width(32), .tristate("true"), .enable("false")) demultiplexer_1 (
    .out1(R1_in), .out2(R2_in), .out3(R3_in), .out4(R4_in), .out5(R5_in), .out6(R6_in), .out7(R7_in),
    .out8(R8_in), .out9(R9_in), .out10(R10_in), .out11(R11_in), .out12(R12_in), .out13(R13_in),
    .out14(R14_in), .out15(R15_in), .out16(R16_in), .out17(R17_in), .out18(R18_in), .out19(R19_in),
    .out20(R20_in), .out21(R21_in), .out22(R22_in), .out23(R23_in), .out24(R24_in), .out25(R25_in),
    .out26(R26_in), .out27(R27_in), .out28(R28_in), .out29(R29_in), .out30(R30_in), .out31(R31_in),
    .in(in_1), .sel(in_7));  // open: out0
  Register #(.width(32)) register_21 (.D(R5_in), .en(in_4), .Q(R5_out), .clk(in_2), .clr(in_3));
  Register #(.width(32)) register_22 (.D(R13_in), .en(in_4), .Q(R13_out), .clk(in_2), .clr(in_3));
  Register #(.width(32)) register_23 (.D(R21_in), .en(in_4), .Q(R21_out), .clk(in_2), .clr(in_3));
  Register #(.width(32)) register_24 (.D(R29_in), .en(in_4), .Q(R29_out), .clk(in_2), .clr(in_3));
  Register #(.width(32)) register_25 (.D(R6_in), .en(in_4), .Q(R6_out), .clk(in_2), .clr(in_3));
  Register #(.width(32)) register_26 (.D(R14_in), .en(in_4), .Q(R14_out), .clk(in_2), .clr(in_3));
  Register #(.width(32)) register_27 (.D(R22_in), .en(in_4), .Q(R22_out), .clk(in_2), .clr(in_3));
  Register #(.width(32)) register_28 (.D(R30_in), .en(in_4), .Q(R30_out), .clk(in_2), .clr(in_3));
  Register #(.width(32)) register_29 (.D(R7_in), .en(in_4), .Q(R7_out), .clk(in_2), .clr(in_3));
  Register #(.width(32)) register_30 (.D(R15_in), .en(in_4), .Q(R15_out), .clk(in_2), .clr(in_3));
  Register #(.width(32)) register_31 (.D(R23_in), .en(in_4), .Q(R23_out), .clk(in_2), .clr(in_3));
  Register #(.width(32)) register_32 (.D(R31_in), .en(in_4), .Q(R31_out), .clk(in_2), .clr(in_3));

  // Other names for the same wires on the sheet: A1[4:0] = in_5; A2[4:0] = in_6; A3[4:0] = in_7; clk = in_2;
  //   RD1[31:0] = out_8; RD2[31:0] = out_9; reset = in_3; WD[31:0] = in_1; WE = in_4
endmodule

module Controller (
  input  [5:0] in_1,
  input  [5:0] in_2,
  output [1:0] out_3,
  output [3:0] out_4,
  output out_5,
  output out_6,
  output out_7,
  output out_8,
  output out_9,
  output out_10,
  output out_11
);

  wire add, \and , beq, boal, comparator_1_eq, comparator_10_eq, comparator_11_eq, comparator_12_eq,
       comparator_13_eq, j, jal, lui, lw, ori, priority_encoder_1_gs, slt, sub, sw;
  wire [3:0] priority_encoder_1_out;

  Comparator #(.width(6)) comparator_1 (.a(in_1), .b({6{1'b0}}), .eq(comparator_1_eq));  // open: gt, lt
  Comparator #(.width(6)) comparator_2 (.a(in_1), .b(6'b001101), .eq(ori));  // open: gt, lt
  Comparator #(.width(6)) comparator_3 (.a(in_1), .b(6'b000100), .eq(beq));  // open: gt, lt
  Comparator #(.width(6)) comparator_4 (.a(in_1), .b(6'b001111), .eq(lui));  // open: gt, lt
  Comparator #(.width(6)) comparator_5 (.a(in_1), .b(6'b101011), .eq(sw));  // open: gt, lt
  Comparator #(.width(6)) comparator_6 (.a(in_1), .b(6'b100011), .eq(lw));  // open: gt, lt
  Comparator #(.width(6)) comparator_7 (.a(in_1), .b(6'b000010), .eq(j));  // open: gt, lt
  Comparator #(.width(6)) comparator_8 (.a(in_1), .b(6'b000011), .eq(jal));  // open: gt, lt
  Comparator #(.width(6)) comparator_9 (.a(in_1), .b(6'b011001), .eq(boal));  // open: gt, lt
  Priority_Encoder #(.select(4)) priority_encoder_1 (
    .in1(ori), .in2(beq), .in3(lui), .in4(sw), .in5(lw), .in6(sub), .in7(add), .in8(slt), .in9(j),
    .in10(\and ), .in11(jal), .in12(boal), .out(priority_encoder_1_out), .gs(priority_encoder_1_gs));  // open: in0, in13, in14, in15, en_out, en_in
  Multiplexer #(.width(4), .enable("false")) multiplexer_1 (
    .in0(4'b0000), .in1(priority_encoder_1_out), .out(out_4), .sel(priority_encoder_1_gs));
  Comparator #(.width(6)) comparator_10 (.a(in_2), .b(6'b100010), .eq(comparator_10_eq));  // open: gt, lt
  Comparator #(.width(6)) comparator_11 (.a(in_2), .b(6'b100000), .eq(comparator_11_eq));  // open: gt, lt
  Comparator #(.width(6)) comparator_12 (.a(in_2), .b(6'b101010), .eq(comparator_12_eq));  // open: gt, lt
  Comparator #(.width(6)) comparator_13 (.a(in_2), .b(6'b100100), .eq(comparator_13_eq));  // open: gt, lt
  Multiplexer #(.select(4), .width(2), .enable("false")) multiplexer_2 (
    .in0(2'b00), .in1(2'b00), .in2(2'b01), .in3(2'b00), .in4(2'b00), .in5(2'b00), .in6(2'b00), .in7(2'b00),
    .in8(2'b00), .in9(2'b10), .in10(2'b00), .in11(2'b10), .in12(2'b11), .out(out_3), .sel(out_4));  // open: in13, in14, in15
  Multiplexer #(.select(4), .enable("false")) multiplexer_3 (
    .in0(1'b0), .in1(1'b1), .in2(1'b0), .in3(1'b1), .in4(1'b0), .in5(1'b1), .in6(1'b1), .in7(1'b1),
    .in8(1'b1), .in9(1'b0), .in10(1'b1), .in11(1'b1), .in12(1'b1), .out(out_7), .sel(out_4));  // open: in13, in14, in15
  and and_1 (sub, comparator_1_eq, comparator_10_eq);
  and and_2 (add, comparator_1_eq, comparator_11_eq);
  and and_3 (slt, comparator_1_eq, comparator_12_eq);
  and and_4 (\and , comparator_1_eq, comparator_13_eq);
  Multiplexer #(.select(4), .enable("false")) multiplexer_4 (
    .in0(1'b0), .in1(1'b0), .in2(1'b0), .in3(1'b0), .in4(1'b1), .in5(1'b1), .in6(1'b0), .in7(1'b0),
    .in8(1'b0), .in9(1'b0), .in10(1'b0), .in11(1'b0), .in12(1'b0), .out(out_8), .sel(out_4));  // open: in13, in14, in15
  Multiplexer #(.select(4), .enable("false")) multiplexer_5 (
    .in0(1'b0), .in1(1'b1), .in2(1'b0), .in3(1'b1), .in4(1'b1), .in5(1'b1), .in6(1'b0), .in7(1'b0),
    .in8(1'b0), .in9(1'b0), .in10(1'b0), .in11(1'b0), .in12(1'b0), .out(out_9), .sel(out_4));  // open: in13, in14, in15
  Multiplexer #(.select(4), .enable("false")) multiplexer_6 (
    .in0(1'b0), .in1(1'b0), .in2(1'b0), .in3(1'b0), .in4(1'b0), .in5(1'b0), .in6(1'b1), .in7(1'b1),
    .in8(1'b1), .in9(1'b0), .in10(1'b1), .in11(1'b1), .in12(1'b1), .out(out_5), .sel(out_4));  // open: in13, in14, in15
  Multiplexer #(.select(4), .enable("false")) multiplexer_7 (
    .in0(1'b0), .in1(1'b0), .in2(1'b0), .in3(1'b0), .in4(1'b1), .in5(1'b0), .in6(1'b0), .in7(1'b0),
    .in8(1'b0), .in9(1'b0), .in10(1'b0), .in11(1'b0), .in12(1'b0), .out(out_10), .sel(out_4));  // open: in13, in14, in15
  Multiplexer #(.select(4), .enable("false")) multiplexer_8 (
    .in0(1'b0), .in1(1'b0), .in2(1'b0), .in3(1'b0), .in4(1'b0), .in5(1'b1), .in6(1'b0), .in7(1'b0),
    .in8(1'b0), .in9(1'b0), .in10(1'b0), .in11(1'b0), .in12(1'b0), .out(out_6), .sel(out_4));  // open: in13, in14, in15
  Multiplexer #(.select(4), .enable("false")) multiplexer_9 (
    .in0(1'b0), .in1(1'b0), .in2(1'b0), .in3(1'b0), .in4(1'b0), .in5(1'b0), .in6(1'b0), .in7(1'b0),
    .in8(1'b0), .in9(1'b0), .in10(1'b0), .in11(1'b1), .in12(1'b0), .out(out_11), .sel(out_4));  // open: in13, in14, in15

  // Other names for the same wires on the sheet: Addr2Reg = out_11; ALUSrc = out_9; EXTOp = out_8; Funct[5:0] = in_2;
  //   Mem2Reg = out_6; MemWr = out_10; NPC_Sel[1:0] = out_3; OpCode[5:0] = in_1; RegDst = out_5; RFWr = out_7;
  //   type[3:0] = out_4
endmodule

module ALU (
  input  [31:0] in_1,
  input  [31:0] in_2,
  input  [3:0] in_3,
  output [31:0] out_4,
  output out_5,
  output out_6
);

  wire _1___2;
  wire [5:0] countones_1_out_2, countones_2_out_2;
  wire [31:0] add, \and , lui, \or , slt, sub;

  Adder #(.width(32)) adder_1 (.a(in_1), .b(in_2), .out(add));  // open: cin, cout
  Subtractor #(.width(32)) subtractor_1 (.a(in_1), .b(in_2), .out(sub));  // open: bin, bout
  Comparator #(.width(32)) comparator_1 (.a(sub), .b({32{1'b0}}), .eq(out_5));  // open: gt, lt
  assign \or  = in_1 | in_2;  // OR_Gate or_1, 32 bits wide
  Shifter #(.width(32)) shifter_1 (.in(in_2), .\dist (5'b10000), .out(lui));
  Comparator #(.width(32)) comparator_2 (.a(in_1), .b(in_2), .lt(_1___2));  // open: gt, eq
  assign \and  = in_1 & in_2;  // AND_Gate and_1, 32 bits wide
  CountOnes countones_1 (.in_1(in_1), .out_2(countones_1_out_2));
  Comparator #(.width(6), .mode("unsigned")) comparator_3 (
    .a(countones_1_out_2), .b(countones_2_out_2), .eq(out_6));  // open: gt, lt
  CountOnes countones_2 (.in_1(in_2), .out_2(countones_2_out_2));
  assign slt = {{31{1'b0}}, _1___2};  // Bit_Extender bit_extender_1
  Multiplexer #(.select(4), .width(32), .enable("false")) multiplexer_1 (
    .in1(\or ), .in3(lui), .in4(add), .in5(add), .in6(sub), .in7(add), .in8(slt), .in10(\and ), .out(out_4),
    .sel(in_3));  // open: in0, in2, in9, in11, in12, in13, in14, in15

  // Other names for the same wires on the sheet: equal = out_6; operand1[31:0] = in_1; operand2[31:0] = in_2;
  //   result[31:0] = out_4; type[3:0] = in_3; zero = out_5
endmodule

module EXT (
  input  [15:0] in_1,
  input  in_2,
  output [31:0] out_3
);

  wire [31:0] bit_extender_1_out, bit_extender_2_out;

  assign bit_extender_1_out = {{16{1'b0}}, in_1};  // Bit_Extender bit_extender_1
  assign bit_extender_2_out = {{16{in_1[15]}}, in_1};  // Bit_Extender bit_extender_2
  Multiplexer #(.width(32), .enable("false")) multiplexer_1 (
    .in0(bit_extender_1_out), .in1(bit_extender_2_out), .out(out_3), .sel(in_2));
endmodule

module DM (
  input  [31:0] in_1,
  input  [31:0] in_2,
  input  in_3,
  input  in_4,
  input  in_5,
  output [31:0] out_6
);

  RAM #(.addrWidth(12), .dataWidth(32), .bus("separate")) ram_1 (
    .addr(in_1[13:2]), .din(in_2), .data(out_6), .str(in_3), .clk(in_4), .clr(in_5));  // open: sel, ld

  // Other names for the same wires on the sheet: Addr[31:0] = in_1; clk = in_4; reset = in_5; WD[31:0] = in_2;
  //   WE = in_3
endmodule

module CountOnes (
  input  [31:0] in_1,
  output [5:0] out_2
);

  wire [4:0] adder_1_out, adder_2_out, adder_3_out, adder_4_out, adder_5_out, adder_6_out, adder_7_out,
       adder_8_out, adder_9_out, adder_10_out, adder_11_out, adder_12_out, adder_13_out, adder_14_out,
       adder_15_out, adder_16_out, adder_17_out, adder_18_out, adder_19_out, adder_20_out, adder_21_out,
       adder_22_out, adder_23_out, adder_24_out, adder_25_out, adder_26_out, adder_27_out, adder_28_out,
       adder_29_out, adder_30_out, bit_extender_1_out, bit_extender_2_out, bit_extender_3_out,
       bit_extender_4_out, bit_extender_5_out, bit_extender_6_out, bit_extender_7_out, bit_extender_8_out,
       bit_extender_9_out, bit_extender_10_out, bit_extender_11_out, bit_extender_12_out,
       bit_extender_13_out, bit_extender_14_out, bit_extender_15_out, bit_extender_16_out,
       bit_extender_17_out, bit_extender_18_out, bit_extender_19_out, bit_extender_20_out,
       bit_extender_21_out, bit_extender_22_out, bit_extender_23_out, bit_extender_24_out,
       bit_extender_25_out, bit_extender_26_out, bit_extender_27_out, bit_extender_28_out,
       bit_extender_29_out, bit_extender_30_out, bit_extender_31_out, bit_extender_32_out;
  wire [5:0] bit_extender_33_out, bit_extender_34_out;

  assign bit_extender_1_out = {{4{1'b0}}, in_1[0]};  // Bit_Extender bit_extender_1
  assign bit_extender_2_out = {{4{1'b0}}, in_1[1]};  // Bit_Extender bit_extender_2
  assign bit_extender_3_out = {{4{1'b0}}, in_1[2]};  // Bit_Extender bit_extender_3
  assign bit_extender_4_out = {{4{1'b0}}, in_1[3]};  // Bit_Extender bit_extender_4
  assign bit_extender_5_out = {{4{1'b0}}, in_1[4]};  // Bit_Extender bit_extender_5
  assign bit_extender_6_out = {{4{1'b0}}, in_1[5]};  // Bit_Extender bit_extender_6
  assign bit_extender_7_out = {{4{1'b0}}, in_1[6]};  // Bit_Extender bit_extender_7
  assign bit_extender_8_out = {{4{1'b0}}, in_1[7]};  // Bit_Extender bit_extender_8
  assign bit_extender_9_out = {{4{1'b0}}, in_1[8]};  // Bit_Extender bit_extender_9
  assign bit_extender_10_out = {{4{1'b0}}, in_1[9]};  // Bit_Extender bit_extender_10
  assign bit_extender_11_out = {{4{1'b0}}, in_1[10]};  // Bit_Extender bit_extender_11
  assign bit_extender_12_out = {{4{1'b0}}, in_1[11]};  // Bit_Extender bit_extender_12
  assign bit_extender_13_out = {{4{1'b0}}, in_1[12]};  // Bit_Extender bit_extender_13
  assign bit_extender_14_out = {{4{1'b0}}, in_1[13]};  // Bit_Extender bit_extender_14
  assign bit_extender_15_out = {{4{1'b0}}, in_1[14]};  // Bit_Extender bit_extender_15
  assign bit_extender_16_out = {{4{1'b0}}, in_1[15]};  // Bit_Extender bit_extender_16
  assign bit_extender_17_out = {{4{1'b0}}, in_1[16]};  // Bit_Extender bit_extender_17
  assign bit_extender_18_out = {{4{1'b0}}, in_1[17]};  // Bit_Extender bit_extender_18
  assign bit_extender_19_out = {{4{1'b0}}, in_1[18]};  // Bit_Extender bit_extender_19
  assign bit_extender_20_out = {{4{1'b0}}, in_1[19]};  // Bit_Extender bit_extender_20
  assign bit_extender_21_out = {{4{1'b0}}, in_1[20]};  // Bit_Extender bit_extender_21
  assign bit_extender_22_out = {{4{1'b0}}, in_1[21]};  // Bit_Extender bit_extender_22
  assign bit_extender_23_out = {{4{1'b0}}, in_1[22]};  // Bit_Extender bit_extender_23
  assign bit_extender_24_out = {{4{1'b0}}, in_1[23]};  // Bit_Extender bit_extender_24
  assign bit_extender_25_out = {{4{1'b0}}, in_1[24]};  // Bit_Extender bit_extender_25
  assign bit_extender_26_out = {{4{1'b0}}, in_1[25]};  // Bit_Extender bit_extender_26
  assign bit_extender_27_out = {{4{1'b0}}, in_1[26]};  // Bit_Extender bit_extender_27
  assign bit_extender_28_out = {{4{1'b0}}, in_1[27]};  // Bit_Extender bit_extender_28
  assign bit_extender_29_out = {{4{1'b0}}, in_1[28]};  // Bit_Extender bit_extender_29
  assign bit_extender_30_out = {{4{1'b0}}, in_1[29]};  // Bit_Extender bit_extender_30
  assign bit_extender_31_out = {{4{1'b0}}, in_1[30]};  // Bit_Extender bit_extender_31
  assign bit_extender_32_out = {{4{1'b0}}, in_1[31]};  // Bit_Extender bit_extender_32
  Adder #(.width(5)) adder_1 (.a(bit_extender_1_out), .b(bit_extender_2_out), .out(adder_1_out));  // open: cin, cout
  Adder #(.width(5)) adder_2 (.a(bit_extender_3_out), .b(bit_extender_4_out), .out(adder_2_out));  // open: cin, cout
  Adder #(.width(5)) adder_3 (.a(bit_extender_5_out), .b(bit_extender_6_out), .out(adder_3_out));  // open: cin, cout
  Adder #(.width(5)) adder_4 (.a(bit_extender_7_out), .b(bit_extender_8_out), .out(adder_4_out));  // open: cin, cout
  Adder #(.width(5)) adder_5 (.a(bit_extender_9_out), .b(bit_extender_10_out), .out(adder_5_out));  // open: cin, cout
  Adder #(.width(5)) adder_6 (.a(bit_extender_11_out), .b(bit_extender_12_out), .out(adder_6_out));  // open: cin, cout
  Adder #(.width(5)) adder_7 (.a(bit_extender_13_out), .b(bit_extender_14_out), .out(adder_7_out));  // open: cin, cout
  Adder #(.width(5)) adder_8 (.a(bit_extender_15_out), .b(bit_extender_16_out), .out(adder_8_out));  // open: cin, cout
  Adder #(.width(5)) adder_9 (.a(bit_extender_17_out), .b(bit_extender_18_out), .out(adder_9_out));  // open: cin, cout
  Adder #(.width(5)) adder_10 (
    .a(bit_extender_19_out), .b(bit_extender_20_out), .out(adder_10_out));  // open: cin, cout
  Adder #(.width(5)) adder_11 (
    .a(bit_extender_21_out), .b(bit_extender_22_out), .out(adder_11_out));  // open: cin, cout
  Adder #(.width(5)) adder_12 (
    .a(bit_extender_23_out), .b(bit_extender_24_out), .out(adder_12_out));  // open: cin, cout
  Adder #(.width(5)) adder_13 (
    .a(bit_extender_25_out), .b(bit_extender_26_out), .out(adder_13_out));  // open: cin, cout
  Adder #(.width(5)) adder_14 (
    .a(bit_extender_27_out), .b(bit_extender_28_out), .out(adder_14_out));  // open: cin, cout
  Adder #(.width(5)) adder_15 (
    .a(bit_extender_29_out), .b(bit_extender_30_out), .out(adder_15_out));  // open: cin, cout
  Adder #(.width(5)) adder_16 (
    .a(bit_extender_31_out), .b(bit_extender_32_out), .out(adder_16_out));  // open: cin, cout
  Adder #(.width(5)) adder_17 (.a(adder_1_out), .b(adder_2_out), .out(adder_17_out));  // open: cin, cout
  Adder #(.width(5)) adder_18 (.a(adder_3_out), .b(adder_4_out), .out(adder_18_out));  // open: cin, cout
  Adder #(.width(5)) adder_19 (.a(adder_5_out), .b(adder_6_out), .out(adder_19_out));  // open: cin, cout
  Adder #(.width(5)) adder_20 (.a(adder_7_out), .b(adder_8_out), .out(adder_20_out));  // open: cin, cout
  Adder #(.width(5)) adder_21 (.a(adder_9_out), .b(adder_10_out), .out(adder_21_out));  // open: cin, cout
  Adder #(.width(5)) adder_22 (.a(adder_11_out), .b(adder_12_out), .out(adder_22_out));  // open: cin, cout
  Adder #(.width(5)) adder_23 (.a(adder_13_out), .b(adder_14_out), .out(adder_23_out));  // open: cin, cout
  Adder #(.width(5)) adder_24 (.a(adder_15_out), .b(adder_16_out), .out(adder_24_out));  // open: cin, cout
  Adder #(.width(5)) adder_25 (.a(adder_17_out), .b(adder_18_out), .out(adder_25_out));  // open: cin, cout
  Adder #(.width(5)) adder_26 (.a(adder_25_out), .b(adder_27_out), .out(adder_26_out));  // open: cin, cout
  Adder #(.width(5)) adder_27 (.a(adder_19_out), .b(adder_20_out), .out(adder_27_out));  // open: cin, cout
  Adder #(.width(5)) adder_28 (.a(adder_21_out), .b(adder_22_out), .out(adder_28_out));  // open: cin, cout
  Adder #(.width(5)) adder_29 (.a(adder_28_out), .b(adder_30_out), .out(adder_29_out));  // open: cin, cout
  Adder #(.width(5)) adder_30 (.a(adder_23_out), .b(adder_24_out), .out(adder_30_out));  // open: cin, cout
  assign bit_extender_33_out = {{1{1'b0}}, adder_26_out};  // Bit_Extender bit_extender_33
  assign bit_extender_34_out = {{1{1'b0}}, adder_29_out};  // Bit_Extender bit_extender_34
  Adder #(.width(6)) adder_31 (.a(bit_extender_33_out), .b(bit_extender_34_out), .out(out_2));  // open: cin, cout
endmodule
