// Logisim project serial_addition.circ as structural Verilog
module serial_addition (
  input  in_1,
  input  in_2,
  input  [1:0] in_3,
  output out_4
);

  wire comparator_1_eq, comparator_1_gt, or_1_out, or_2_out, register_2_q;
  wire [2:0] cache, middle, multiplexer_1_out, multiplexer_3_out;

  Multiplexer #(.select(2), .width(3), .enable("false")) multiplexer_1 (
    .in0(3'b001), .in2(3'b010), .in3(3'b011), .out(multiplexer_1_out), .sel(in_3));  // open: in1
  or or_1 (or_1_out, comparator_1_gt, comparator_1_eq);
  Comparator #(.width(3), .mode("unsigned")) comparator_1 (
    .a(middle), .b(3'b101), .gt(comparator_1_gt), .eq(comparator_1_eq));  // open: lt
  Adder #(.width(3)) adder_1 (.a(cache), .b(multiplexer_1_out), .out(middle));  // open: cin, cout
  or or_2 (or_2_out, in_2, out_4);
  Multiplexer #(.enable("false")) multiplexer_2 (.in0(or_1_out), .in1(1'b0), .out(out_4), .sel(in_2));
  Multiplexer #(.width(3), .enable("false")) multiplexer_3 (
    .in0(middle), .in1(3'b000), .out(multiplexer_3_out), .sel(or_2_out));
  Register #(.width(3)) register_1 (.D(multiplexer_3_out), .Q(cache), .clk(in_1));  // open: en, clr
  Register #(.width(1)) register_2 (.Q(register_2_q));  // open: D, en, clk, clr

  // Other names for the same wires on the sheet: clk = in_1; clr = in_2; in[1:0] = in_3; out = out_4; reset = out_4
endmodule

module serial_addition2 (
  input  in_1,
  input  in_2,
  input  [1:0] in_3,
  output out_4
);

  wire comparator_1_eq, comparator_1_gt, or_1_out, or_2_out, reset;
  wire [2:0] cache, middle, multiplexer_1_out, multiplexer_3_out;

  Multiplexer #(.select(2), .width(3), .enable("false")) multiplexer_1 (
    .in0(3'b001), .in2(3'b010), .in3(3'b011), .out(multiplexer_1_out), .sel(in_3));  // open: in1
  or or_1 (or_1_out, comparator_1_gt, comparator_1_eq);
  Comparator #(.width(3), .mode("unsigned")) comparator_1 (
    .a(middle), .b(3'b101), .gt(comparator_1_gt), .eq(comparator_1_eq));  // open: lt
  Adder #(.width(3)) adder_1 (.a(cache), .b(multiplexer_1_out), .out(middle));  // open: cin, cout
  or or_2 (or_2_out, in_2, reset);
  Multiplexer #(.enable("false")) multiplexer_2 (.in0(or_1_out), .in1(1'b0), .out(reset), .sel(in_2));
  Register #(.width(3)) register_1 (.D(multiplexer_3_out), .Q(cache), .clk(in_1));  // open: en, clr
  Multiplexer #(.width(3), .enable("false")) multiplexer_3 (
    .in0(middle), .in1(3'b000), .out(multiplexer_3_out), .sel(or_2_out));
  Register #(.width(1)) register_2 (.D(reset), .Q(out_4), .clk(in_1));  // open: en, clr

  // Other names for the same wires on the sheet: clk = in_1; clr = in_2; in[1:0] = in_3; out = out_4
endmodule
