// Logisim project tetris.circ as structural Verilog
module tetris (
  input  in_1,
  input  in_2,
  input  [7:0] in_3,
  output [1:0] out_4
);

  wire comparator_1_eq, judge_full, judge_not_have, judge_reset, or_1_out;
  wire [1:0] multiplexer_1_out;
  wire [7:0] block, judge;

  or or_1 (or_1_out, in_2, judge_reset);
  assign block = in_3 | judge;  // OR_Gate or_2, 8 bits wide
  Register tetris (.D(block), .Q(judge), .clk(in_1), .clr(or_1_out));  // open: en
  Comparator comparator_1 (.a(block), .b(judge), .eq(comparator_1_eq));  // open: gt, lt
  not not_1 (judge_not_have, comparator_1_eq);
  // Probe on judge
  Multiplexer #(.select(2), .width(2), .enable("false")) multiplexer_1 (
    .in0(2'b00), .in1(2'b01), .in3(2'b10), .out(multiplexer_1_out), .sel({judge_full, judge_not_have}));  // open: in2
  // Probe on {judge_full, judge_not_have}
  Comparator comparator_2 (.a(judge), .b({8{1'b1}}), .eq(judge_reset));  // open: gt, lt
  Comparator comparator_3 (.a(block), .b({8{1'b1}}), .eq(judge_full));  // open: gt, lt
  Register #(.width(2)) register_1 (.D(multiplexer_1_out), .Q(out_4), .clk(in_1), .clr(in_2));  // open: en

  // Other names for the same wires on the sheet: clk = in_1; position[7:0] = in_3; reset = in_2; result[1:0] = out_4

  // Notes on the sheet:
  //   use the loaded value
  //   use the unloaded value to judge whether to display 10
endmodule
