// Logisim project sequence_generator.circ as structural Verilog: 2 circuits, main circuit main
module main (
  input  [1:0] in_1,
  input  in_2,
  input  in_3,
  output [31:0] out_4
);

  wire [31:0] accumulate, adder_1_out, multiplexer_1_out, multiplexer_2_out, prev, store_the_sum_q;

  Adder #(.width(32)) adder_1 (.a(32'h1), .b(out_4), .out(adder_1_out));  // open: cin, cout
  Multiplexer #(.width(32), .enable("false")) multiplexer_1 (
    .in0(adder_1_out), .in1({32{1'b0}}), .out(multiplexer_1_out), .sel(in_2));
  Register #(.width(32)) store_the__1 (.D(multiplexer_1_out), .Q(prev), .clk(in_3));  // open: en, clr
  Register #(.width(32)) store_the_sum (.D(multiplexer_2_out), .Q(store_the_sum_q), .clk(in_3));  // open: en, clr
  Multiplexer #(.width(32), .enable("false")) multiplexer_2 (
    .in0(accumulate), .in1({32{1'b0}}), .out(multiplexer_2_out), .sel(in_2));
  Adder #(.width(32)) adder_2 (.a(store_the_sum_q), .b(out_4), .out(accumulate));  // open: cin, cout
  Multiplexer #(.select(2), .width(32)) multiplexer_3 (
    .in0({32{1'b0}}), .in1(prev), .in2(accumulate), .out(out_4), .sel(in_1));  // open: in3, en

  // Other names for the same wires on the sheet: clk = in_3; output[31:0] = out_4; reset = in_2; type[1:0] = in_1
endmodule

module \sequence  (
  input  [1:0] in_1,
  input  in_2,
  input  in_3,
  output [31:0] out_4
);

  wire [31:0] accumulate, adder_2_out, multiplexer_2_out, multiplexer_3_out, prev, sum;

  Adder #(.width(32)) adder_1 (.a(32'h1), .b(out_4), .out(prev));  // open: cin, cout
  Multiplexer #(.select(2), .width(32)) multiplexer_1 (
    .in0({32{1'b0}}), .in1(prev), .in2(sum), .out(accumulate), .sel(in_1));  // open: in3, en
  Adder #(.width(32)) adder_2 (.a(sum), .b(accumulate), .out(adder_2_out));  // open: cin, cout
  Register #(.width(32)) result (.D(multiplexer_2_out), .Q(out_4), .clk(in_3));  // open: en, clr
  Multiplexer #(.width(32), .enable("false")) multiplexer_2 (
    .in0(accumulate), .in1({32{1'b0}}), .out(multiplexer_2_out), .sel(in_2));
  Multiplexer #(.width(32), .enable("false")) multiplexer_3 (
    .in0(adder_2_out), .in1({32{1'b0}}), .out(multiplexer_3_out), .sel(in_2));
  Register #(.width(32)) result_2 (.D(multiplexer_3_out), .Q(sum), .clk(in_3));  // open: en, clr

  // Other names for the same wires on the sheet: clk = in_3; output[31:0] = out_4; reset = in_2; type[1:0] = in_1

  // Notes on the sheet:
  //   decide the current value and the ouput
  //   store the accumulation value
endmodule
