// Logisim project Sokoban.circ as structural Verilog
module Sokoban (
  input  dx,
  input  dy,
  input  clk,
  input  reset,
  output out_5,
  output out_6
);

  wire not_1_out, not_2_out, wall;
  wire [2:0] bit_extender_1_out, bit_extender_2_out, out_x, out_y, x, y;

  Register #(.width(3)) u_x (.D(x), .en(not_1_out), .Q(out_x), .clk(clk), .clr(reset));
  not not_1 (not_1_out, wall);
  Register #(.width(3)) u_y (.D(y), .en(not_2_out), .Q(out_y), .clk(clk), .clr(reset));
  not not_2 (not_2_out, wall);
  assign bit_extender_1_out = {{2{1'b0}}, dx};  // Bit_Extender bit_extender_1
  assign bit_extender_2_out = {{2{1'b0}}, dy};  // Bit_Extender bit_extender_2
  Adder #(.width(3)) adder_1 (.a(bit_extender_1_out), .b(out_x), .out(x));  // open: cin, cout
  Adder #(.width(3)) adder_2 (.a(bit_extender_2_out), .b(out_y), .out(y));  // open: cin, cout
  wall wall_1 (.in_1(x), .in_2(y), .out_3(wall));
  End end_1 (.in_1(out_x), .in_2(out_y), .out_3(out_6));
  Register #(.width(1)) register_1 (.D(wall), .Q(out_5), .clk(clk), .clr(reset));  // open: en

  // Other names for the same wires on the sheet: flag = out_5; out = out_6
endmodule

module wall (
  input  [2:0] in_1,
  input  [2:0] in_2,
  output out_3
);

  wire and_1_out, and_2_out, and_3_out, and_4_out, and_5_out, and_6_out, comparator_1_eq, comparator_2_eq,
       comparator_3_eq, comparator_4_eq, comparator_5_eq, comparator_6_eq, comparator_7_eq, comparator_8_eq,
       comparator_9_eq, comparator_10_eq, comparator_11_eq, comparator_12_eq, comparator_13_eq,
       comparator_14_eq;

  Comparator #(.width(3)) comparator_1 (.a(in_1), .b(3'b001), .eq(comparator_1_eq));  // open: gt, lt
  Comparator #(.width(3)) comparator_2 (.a(in_2), .b(3'b001), .eq(comparator_2_eq));  // open: gt, lt
  Comparator #(.width(3)) comparator_3 (.a(in_1), .b(3'b001), .eq(comparator_3_eq));  // open: gt, lt
  Comparator #(.width(3)) comparator_4 (.a(in_2), .b(3'b010), .eq(comparator_4_eq));  // open: gt, lt
  Comparator #(.width(3)) comparator_5 (.a(in_1), .b(3'b010), .eq(comparator_5_eq));  // open: gt, lt
  Comparator #(.width(3)) comparator_6 (.a(in_2), .b(3'b001), .eq(comparator_6_eq));  // open: gt, lt
  Comparator #(.width(3)) comparator_7 (.a(3'b110), .b(in_1), .eq(comparator_7_eq));  // open: gt, lt
  Comparator #(.width(3)) comparator_8 (.a(3'b110), .b(in_2), .eq(comparator_8_eq));  // open: gt, lt
  Comparator #(.width(3)) comparator_9 (.a(in_1), .b(3'b011), .eq(comparator_9_eq));  // open: gt, lt
  Comparator #(.width(3)) comparator_10 (.a(in_2), .b(3'b100), .eq(comparator_10_eq));  // open: gt, lt
  Comparator #(.width(3)) comparator_11 (.a(in_1), .b(3'b100), .eq(comparator_11_eq));  // open: gt, lt
  Comparator #(.width(3)) comparator_12 (.a(in_2), .b(3'b011), .eq(comparator_12_eq));  // open: gt, lt
  Comparator #(.width(3)) comparator_13 (.a(in_1), .b(3'b100), .eq(comparator_13_eq));  // open: gt, lt
  Comparator #(.width(3)) comparator_14 (.a(in_2), .b(3'b100), .eq(comparator_14_eq));  // open: gt, lt
  and and_1 (and_1_out, comparator_1_eq, comparator_2_eq);
  and and_2 (and_2_out, comparator_3_eq, comparator_4_eq);
  and and_3 (and_3_out, comparator_5_eq, comparator_6_eq);
  and and_4 (and_4_out, comparator_9_eq, comparator_10_eq);
  and and_5 (and_5_out, comparator_11_eq, comparator_12_eq);
  and and_6 (and_6_out, comparator_13_eq, comparator_14_eq);
  or or_1 (out_3, and_1_out, and_2_out, and_3_out, comparator_7_eq, comparator_8_eq, and_4_out, and_5_out, and_6_out);

  // Other names for the same wires on the sheet: x[2:0] = in_1; y[2:0] = in_2
endmodule

module End (
  input  [2:0] in_1,
  input  [2:0] in_2,
  output out_3
);

  wire comparator_1_eq, comparator_2_eq;

  Comparator #(.width(3)) comparator_1 (.a(3'b101), .b(in_1), .eq(comparator_1_eq));  // open: gt, lt
  Comparator #(.width(3)) comparator_2 (.a(in_2), .b(3'b101), .eq(comparator_2_eq));  // open: gt, lt
  and and_1 (out_3, comparator_1_eq, comparator_2_eq);

  // Other names for the same wires on the sheet: x[2:0] = in_1; y[2:0] = in_2
endmodule
