// Logisim project initial_value.circ as structural Verilog: 1 circuit, main circuit main
module main (
  input  [7:0] in_1,
  output [7:0] out_2
);

  wire clock_1_out;
  wire [7:0] register_1_q, xor_1_out;

  assign xor_1_out = 8'hf ^ in_1;  // XOR_Gate xor_1, 8 bits wide
  Register register_1 (.D(xor_1_out), .Q(register_1_q), .clk(clock_1_out));  // open: en, clr
  Clock clock_1 (.out(clock_1_out));
  assign out_2 = 8'hf ^ register_1_q;  // XOR_Gate xor_2, 8 bits wide

  // Notes on the sheet:
  //   set the output value as inital value
  //   this is the value that we want to store
endmodule
